// Logisim project lab2.3.circ as structural Verilog: 2 circuits, main circuit main
module main (
  input  [3:0] X,
  input  [3:0] Y,
  input  Cin,
  output [3:0] F,
  output Cout
);

  wire and_1_out, FA0_cout, FA1_cout, FA2_cout, FA3_cout, not_1_out, not_2_out, not_3_out, not_4_out;
  wire [3:0] multiplexer_1_out, negator_1_out;

  Hex_Digit_Display hex_digit_display_1 (.value(X), .dp(1'b0));
  Multiplexer #(.width(4), .enable("false")) multiplexer_1 (
    .in0(Y), .in1(negator_1_out), .out(multiplexer_1_out), .sel(Cin));
  Negator #(.width(4)) negator_1 (.in(Y), .out(negator_1_out));
  Hex_Digit_Display hex_digit_display_2 (.value(Y), .dp(1'b0));
  FA FA0 (.A(X[0]), .B(multiplexer_1_out[0]), .Cin(1'b0), .Cout(FA0_cout), .F(F[0]));
  Hex_Digit_Display hex_digit_display_3 (.value(F), .dp(1'b0));
  FA FA1 (.A(X[1]), .B(multiplexer_1_out[1]), .Cin(FA0_cout), .Cout(FA1_cout), .F(F[1]));
  FA FA2 (.A(X[2]), .B(multiplexer_1_out[2]), .Cin(FA1_cout), .Cout(FA2_cout), .F(F[2]));
  not not_1 (not_1_out, multiplexer_1_out[0]);
  not not_2 (not_2_out, multiplexer_1_out[1]);
  and and_1 (and_1_out, not_1_out, not_2_out, not_3_out, not_4_out, Cin);
  not not_3 (not_3_out, multiplexer_1_out[2]);
  not not_4 (not_4_out, multiplexer_1_out[3]);
  FA FA3 (.A(X[3]), .B(multiplexer_1_out[3]), .Cin(FA2_cout), .Cout(FA3_cout), .F(F[3]));
  or or_1 (Cout, FA3_cout, and_1_out);

  // Other names for the same wires on the sheet: SUM[3:0] = F; 操作数x[3:0] = X; 操作数y[3:0] = Y

  // Notes on the sheet:
  //   输入引脚
  //   =
  //   请勿修改引脚名称、电路名称及电路封装外观
  //   提示：使用独立逻辑门及全加器FA子电路实现4位二进制数加减法器，禁止直接使用加减法器组件。
  //   输出引脚
endmodule

module FA (
  input  A,
  input  B,
  input  Cin,
  output F,
  output Cout
);

  wire and_1_out, and_2_out, and_3_out, xor_1_out;

  and and_1 (and_1_out, A, B);
  and and_2 (and_2_out, B, Cin);
  and and_3 (and_3_out, A, Cin);
  xor xor_1 (xor_1_out, A, B);
  xor xor_2 (F, xor_1_out, Cin);
  or or_1 (Cout, and_1_out, and_2_out, and_3_out);

  // Notes on the sheet:
  //   全加器
endmodule
