// Logisim project lab3.2.circ as structural Verilog: 1 circuit, main circuit SHRG4U
module SHRG4U (
  input  CLK,
  input  CLR_L,
  input  RIN,
  input  D3,
  input  D2,
  input  D1,
  input  D0,
  input  LIN,
  input  S1,
  input  S0,
  output Q3,
  output Q2,
  output Q1,
  output Q0
);

  D_Flip_Flop #(.trigger("falling")) QD (.Q(Q3));  // open: clk, D, Qn, preset, reset
  D_Flip_Flop #(.trigger("falling")) QC (.Q(Q2));  // open: clk, D, Qn, preset, reset
  D_Flip_Flop #(.trigger("falling")) QB (.Q(Q1));  // open: clk, D, Qn, preset, reset
  D_Flip_Flop #(.trigger("falling")) QA (.Q(Q0));  // open: clk, D, Qn, preset, reset

  // Notes on the sheet:
  //   输入引脚
  //   请勿修改引脚名称、电路名称及电路封装外观
  //   提示：使用独立逻辑门实现4位异步清零移位寄存器，禁止直接使用移位寄存器组件。
  //   输出引脚
endmodule
