// Logisim project lab3.3.circ as structural Verilog: 5 circuits, main circuit main
module main (
  input  CLK,
  input  [3:0] X,
  input  [3:0] Y,
  input  Reset,
  output [7:0] Prod
);

  wire adder4b_1_cout, LOAD, not_1_out, STOP;
  wire [3:0] \_4位同步计数器_q0 , adder4b_1_f, multiplexer_1_out, multiplexer_2_out;
  wire [7:0] \桶形移位器_dataout ;

  Multiplexer #(.width(4), .enable("false")) multiplexer_1 (
    .in0(4'b0000), .in1(X), .out(multiplexer_1_out), .sel(Prod[0]));
  Hex_Digit_Display hex_digit_display_1 (.value(X));  // open: dp
  not not_1 (not_1_out, STOP);
  ADDER4b adder4b_1 (.X(multiplexer_1_out), .Y(Prod[7:4]), .F(adder4b_1_f), .Cout(adder4b_1_cout), .Cin(1'b0));
  Hex_Digit_Display hex_digit_display_2 (.value(Y));  // open: dp
  Register #(.width(4), .Select("low")) register_1 (
    .D(\桶形移位器_dataout [7:4]), .en(not_1_out), .Q(Prod[7:4]), .clk(CLK), .clr(Reset));
  Hex_Digit_Display hex_digit_display_3 (.value(Prod[7:4]));  // open: dp
  // Probe on nothing
  BarrelSFT8b \u_桶形移位器  (
    .DataIn({adder4b_1_f, Prod[3:0]}), .shamt(3'b001), .L_R(1'b0), .A_L(1'b0), .DataOut(\桶形移位器_dataout ),
    .IN(adder4b_1_cout));
  Hex_Digit_Display hex_digit_display_4 (.value(Prod[3:0]));  // open: dp
  // Probe on nothing
  Register #(.width(4), .Select("low")) Y_2 (
    .D(multiplexer_2_out), .en(not_1_out), .Q(Prod[3:0]), .clk(CLK), .clr(Reset));
  Multiplexer #(.width(4), .enable("false")) multiplexer_2 (
    .in0(\桶形移位器_dataout [3:0]), .in1(Y), .out(multiplexer_2_out), .sel(LOAD));
  // Probe on X
  // Probe on Y
  // Probe on Prod
  CNTR4U \_4位同步计数器  (
    .CLK(CLK), .LD(1'b0), .CLR(Reset), .Q0(\_4位同步计数器_q0 [0]), .Q1(\_4位同步计数器_q0 [1]), .D0(1'b0), .D1(1'b0),
    .D2(1'b0), .Q2(\_4位同步计数器_q0 [2]), .Q3(\_4位同步计数器_q0 [3]), .D3(1'b0), .ENP(1'b1), .ENT(1'b1));  // open: RCO
  Comparator #(.width(4)) comparator_1 (.a(\_4位同步计数器_q0 ), .b(4'b0000), .eq(LOAD));  // open: gt, lt
  Comparator #(.width(4)) comparator_2 (.a(\_4位同步计数器_q0 ), .b(4'b0101), .eq(STOP));  // open: gt, lt

  // Other names for the same wires on the sheet: RST = Reset; Z[7:0] = Prod

  // Notes on the sheet:
  //   X
  //   输入引脚
  //   P
  //   =
  //   请勿修改引脚名称、电路名称及电路封装外观
  //   提示: 采用无符号数一位乘法实现4位二进制乘法器，禁止直接使用乘法器组件
  //   ×
  //   =
  //   输出引脚
endmodule

module CNTR4U (
  input  CLK,
  input  LD,
  input  CLR,
  input  D0,
  input  D1,
  input  D2,
  input  D3,
  input  ENP,
  input  ENT,
  output Q0,
  output Q1,
  output Q2,
  output Q3,
  output RCO
);

  wire and_1_out, and_2_out, and_3_out, and_4_out, and_5_out, and_6_out, and_7_out, and_8_out, and_10_out,
       and_11_out, and_12_out, and_13_out, and_14_out, and_15_out, and_16_out, and_17_out, d_ff_1_qn,
       d_ff_2_qn, d_ff_3_qn, d_ff_4_qn, not_1_out, not_2_out, not_3_out, not_4_out, not_5_out, not_6_out,
       not_7_out, not_8_out, not_9_out, not_10_out, not_11_out, not_12_out, not_13_out, not_14_out,
       not_15_out, not_16_out, not_17_out, not_18_out, not_19_out, not_20_out, not_21_out, not_22_out,
       or_1_out, or_2_out, or_3_out, or_4_out, xor_1_out, xor_2_out, xor_3_out, xor_4_out;

  not not_1 (not_1_out, d_ff_2_qn);
  not not_2 (not_2_out, d_ff_1_qn);
  not not_3 (not_3_out, CLK);
  not not_4 (not_4_out, not_5_out);
  not not_5 (not_5_out, CLR);
  not not_6 (not_6_out, d_ff_1_qn);
  and and_1 (and_1_out, not_1_out, not_2_out);
  not not_7 (not_7_out, d_ff_3_qn);
  and and_2 (and_2_out, not_7_out, not_8_out, not_9_out);
  not not_8 (not_8_out, d_ff_2_qn);
  not not_9 (not_9_out, d_ff_1_qn);
  and and_3 (and_3_out, ENP, ENT);
  not not_10 (not_10_out, ENT);
  not not_11 (not_11_out, not_4_out);
  not not_12 (not_12_out, and_7_out);
  not not_13 (not_13_out, not_4_out);
  xor xor_1 (xor_1_out, and_3_out, not_14_out);
  not not_14 (not_14_out, d_ff_1_qn);
  and and_4 (and_4_out, not_6_out, and_3_out);
  xor xor_2 (xor_2_out, and_4_out, not_15_out);
  not not_15 (not_15_out, d_ff_2_qn);
  and and_5 (and_5_out, and_1_out, and_3_out);
  not not_16 (not_16_out, d_ff_3_qn);
  and and_6 (and_6_out, and_2_out, and_3_out);
  not not_17 (not_17_out, d_ff_4_qn);
  not not_18 (not_18_out, d_ff_4_qn);
  not not_19 (not_19_out, d_ff_3_qn);
  not not_20 (not_20_out, d_ff_2_qn);
  not not_21 (not_21_out, d_ff_1_qn);
  not not_22 (not_22_out, not_10_out);
  and and_7 (and_7_out, LD, not_11_out);
  and and_8 (and_8_out, not_12_out, not_13_out);
  xor xor_3 (xor_3_out, and_5_out, not_16_out);
  xor xor_4 (xor_4_out, and_6_out, not_17_out);
  and and_9 (RCO, not_18_out, not_19_out, not_20_out, not_21_out, not_22_out);
  and and_10 (and_10_out, and_7_out, D0);
  and and_11 (and_11_out, and_8_out, xor_1_out);
  and and_12 (and_12_out, and_7_out, D1);
  and and_13 (and_13_out, and_8_out, xor_2_out);
  and and_14 (and_14_out, and_7_out, D2);
  and and_15 (and_15_out, and_8_out, xor_3_out);
  and and_16 (and_16_out, and_7_out, D3);
  and and_17 (and_17_out, and_8_out, xor_4_out);
  or or_1 (or_1_out, and_10_out, and_11_out);
  or or_2 (or_2_out, and_12_out, and_13_out);
  or or_3 (or_3_out, and_14_out, and_15_out);
  or or_4 (or_4_out, and_16_out, and_17_out);
  D_Flip_Flop #(.trigger("falling")) d_ff_1 (
    .clk(not_3_out), .D(or_1_out), .Q(Q0), .Qn(d_ff_1_qn));  // open: preset, reset
  D_Flip_Flop #(.trigger("falling")) d_ff_2 (
    .clk(not_3_out), .D(or_2_out), .Q(Q1), .Qn(d_ff_2_qn));  // open: preset, reset
  D_Flip_Flop #(.trigger("falling")) d_ff_3 (
    .clk(not_3_out), .D(or_3_out), .Q(Q2), .Qn(d_ff_3_qn));  // open: preset, reset
  D_Flip_Flop #(.trigger("falling")) d_ff_4 (
    .clk(not_3_out), .D(or_4_out), .Q(Q3), .Qn(d_ff_4_qn));  // open: preset, reset

  // Notes on the sheet:
  //   输入引脚
  //   请勿修改引脚名称、电路名称及电路封装外观
  //   提示：使用独立逻辑门实现4位二进制同步计数器，禁止直接使用计数器组件。
  //   输出引脚
endmodule

module ADDER4b (
  input  [3:0] X,
  input  [3:0] Y,
  input  Cin,
  output [3:0] F,
  output Cout
);

  wire fa_1_cout, fa_2_cout, fa_3_cout;
  wire [3:0] bit_extender_1_out, xor_1_out;

  assign bit_extender_1_out = {{3{Cin}}, Cin};  // Bit_Extender bit_extender_1
  Hex_Digit_Display hex_digit_display_1 (.value(X), .dp(1'b0));
  assign xor_1_out = bit_extender_1_out ^ Y;  // XOR_Gate xor_1, 4 bits wide
  Hex_Digit_Display hex_digit_display_2 (.value(xor_1_out), .dp(1'b0));
  FA fa_1 (.A(X[0]), .B(xor_1_out[0]), .Cin(Cin), .F(F[0]), .Cout(fa_1_cout));
  Hex_Digit_Display hex_digit_display_3 (.value(F), .dp(1'b0));
  FA fa_2 (.A(X[1]), .B(xor_1_out[1]), .Cin(fa_1_cout), .F(F[1]), .Cout(fa_2_cout));
  FA fa_3 (.A(X[2]), .B(xor_1_out[2]), .Cin(fa_2_cout), .F(F[2]), .Cout(fa_3_cout));
  FA fa_4 (.A(X[3]), .B(xor_1_out[3]), .Cin(fa_3_cout), .F(F[3]), .Cout(Cout));

  // Other names for the same wires on the sheet: SUM[3:0] = F; 操作数x[3:0] = X; 操作数y[3:0] = Y

  // Notes on the sheet:
  //   输入引脚
  //   +
  //   =
  //   请勿修改引脚名称、电路名称及电路封装外观
  //   提示：使用独立逻辑门及全加器FA子电路实现4位二进制数加减法器，禁止直接使用加减法器组件。
  //   输出引脚
endmodule

module FA (
  input  A,
  input  B,
  input  Cin,
  output F,
  output Cout
);

  wire and_1_out, and_2_out, and_3_out;

  xor xor_1 (F, A, B, Cin);
  and and_1 (and_1_out, A, B);
  and and_2 (and_2_out, B, Cin);
  and and_3 (and_3_out, A, Cin);
  or or_1 (Cout, and_1_out, and_2_out, and_3_out);

  // Notes on the sheet:
  //   全加器
endmodule

module BarrelSFT8b (
  input  [7:0] DataIn,
  input  [2:0] shamt,
  input  IN,
  input  L_R,
  input  A_L,
  output [7:0] DataOut
);

  wire [0:0] multiplexer_2_out;
  wire [1:0] multiplexer_4_out;
  wire [3:0] multiplexer_5_out, multiplexer_6_out;
  wire [7:0] multiplexer_1_out, multiplexer_3_out;

  Multiplexer #(.enable("false")) multiplexer_1 (.in0(IN), .in1(DataIn[7]), .out(multiplexer_1_out[7]), .sel(A_L));
  Multiplexer #(.enable("false")) multiplexer_2 (.in0(IN), .in1(DataIn[7]), .out(multiplexer_2_out[0]), .sel(A_L));
  Multiplexer #(.select(2), .width(8), .enable("false")) multiplexer_3 (
    .in0(DataIn), .in1({multiplexer_1_out[7], DataIn[7:1]}), .in2(DataIn),
    .in3({DataIn[6:0], multiplexer_2_out[0]}), .out(multiplexer_3_out), .sel({L_R, shamt[0]}));
  Multiplexer #(.width(2), .enable("false")) multiplexer_4 (
    .in0(2'b00), .in1(multiplexer_3_out[7:6]), .out(multiplexer_4_out), .sel(A_L));
  Multiplexer #(.select(2), .width(8), .enable("false")) multiplexer_5 (
    .in0(multiplexer_3_out), .in1({{2{multiplexer_1_out[7]}}, multiplexer_3_out[7:2]}),
    .in2(multiplexer_3_out), .in3({multiplexer_3_out[5:0], multiplexer_4_out}),
    .out({multiplexer_1_out[3:0], multiplexer_5_out}), .sel({L_R, shamt[1]}));
  Multiplexer #(.width(4), .enable("false")) multiplexer_6 (
    .in0(4'b0000), .in1(multiplexer_1_out[3:0]), .out(multiplexer_6_out), .sel(A_L));
  Multiplexer #(.select(2), .width(8), .enable("false")) multiplexer_7 (
    .in0({multiplexer_1_out[3:0], multiplexer_5_out}),
    .in1({{4{multiplexer_1_out[7]}}, multiplexer_1_out[3:0]}),
    .in2({multiplexer_1_out[3:0], multiplexer_5_out}), .in3({multiplexer_5_out, multiplexer_6_out}),
    .out(DataOut), .sel({L_R, shamt[2]}));

  // Other names for the same wires on the sheet: Din[7:0] = DataIn; Left_Right = L_R; Arth_Logic = A_L;
  //   Dout[7:0] = DataOut; Input = IN

  // Notes on the sheet:
  //   L/R,A/L: 00逻辑右移，01算术右移，10逻辑左移，11：循环左移
  //   输入引脚
  //   请勿修改引脚名称、电路名称及电路封装外观
  //   提示：使用多路选择器级联实现8位桶形移位器，禁止直接使用移位器组件。
  //   输出引脚
endmodule
