// Logisim project lab3.5.circ as structural Verilog: 1 circuit, main circuit main
module main (
  input  CLK,
  input  LD,
  input  [3:0] HH1,
  input  [3:0] HH0,
  input  [3:0] MM1,
  input  [3:0] MM0,
  input  [3:0] SS1,
  input  [3:0] SS0,
  output [3:0] HH_H,
  output [3:0] HH_L,
  output [3:0] MM_H,
  output [3:0] MM_L,
  output [3:0] SS_H,
  output [3:0] SS_L,
  output LED_R,
  output LED_G,
  output LED_B,
  output INErr
);

  wire and_1_out, and_2_out, and_3_out, and_4_out, and_6_out, and_8_out, and_9_out, and_10_out, and_11_out,
       and_12_out, comparator_1_eq, comparator_1_gt, comparator_2_gt, comparator_3_gt, comparator_4_eq,
       comparator_4_gt, comparator_5_gt, comparator_6_eq, comparator_6_gt, comparator_7_eq, comparator_8_eq,
       comparator_9_eq, comparator_10_eq, comparator_10_lt, comparator_12_eq, comparator_13_eq,
       comparator_14_eq, comparator_15_eq, comparator_16_eq, comparator_17_eq, comparator_18_eq,
       comparator_19_eq, comparator_20_eq, comparator_21_eq, comparator_22_eq, LED_EN, not_1_out, or_1_out,
       or_2_out, or_3_out, or_4_out, or_5_out, START, STOP, xor_1_out, xor_2_out;
  wire [3:0] cntr4u_4_q0;

  and and_1 (and_1_out, LD, not_1_out);
  not not_1 (not_1_out, INErr);
  Comparator #(.width(4), .mode("unsigned")) comparator_1 (
    .a(HH1), .b(4'b0010), .gt(comparator_1_gt), .eq(comparator_1_eq));  // open: lt
  Comparator #(.width(4), .mode("unsigned")) comparator_2 (.a(HH0), .b(4'b0011), .gt(comparator_2_gt));  // open: eq, lt
  Comparator #(.width(4), .mode("unsigned")) comparator_3 (.a(MM1), .b(4'b0101), .gt(comparator_3_gt));  // open: eq, lt
  Comparator #(.width(4), .mode("unsigned")) comparator_4 (
    .a(MM0), .b(4'b1001), .gt(comparator_4_gt), .eq(comparator_4_eq));  // open: lt
  Comparator #(.width(4), .mode("unsigned")) comparator_5 (.a(SS1), .b(4'b0101), .gt(comparator_5_gt));  // open: eq, lt
  Comparator #(.width(4), .mode("unsigned")) comparator_6 (
    .a(SS0), .b(4'b1001), .gt(comparator_6_gt), .eq(comparator_6_eq));  // open: lt
  and and_2 (and_2_out, comparator_1_eq, comparator_2_gt);
  Hex_Digit_Display hex_digit_display_1 (.value(HH_H));  // open: dp
  CNTR4U cntr4u_1 (
    .CLK(CLK), .LD(and_1_out), .CLR(and_8_out), .Q0(HH_H[0]), .Q1(HH_H[1]), .D0(HH1[0]), .D1(HH1[1]),
    .D2(HH1[2]), .Q2(HH_H[2]), .Q3(HH_H[3]), .D3(HH1[3]), .ENP(comparator_12_eq), .ENT(comparator_12_eq));  // open: RCO
  CNTR4U cntr4u_2 (
    .CLK(CLK), .LD(and_1_out), .CLR(LED_EN), .Q0(MM_H[0]), .Q1(MM_H[1]), .D0(MM1[0]), .D1(MM1[1]),
    .D2(MM1[2]), .Q2(MM_H[2]), .Q3(MM_H[3]), .D3(MM1[3]), .ENP(and_9_out), .ENT(and_9_out));  // open: RCO
  CNTR4U cntr4u_3 (
    .CLK(CLK), .LD(and_1_out), .CLR(and_6_out), .Q0(SS_H[0]), .Q1(SS_H[1]), .D0(SS1[0]), .D1(SS1[1]),
    .D2(SS1[2]), .Q2(SS_H[2]), .Q3(SS_H[3]), .D3(SS1[3]), .ENP(comparator_15_eq), .ENT(comparator_15_eq));  // open: RCO
  or or_1 (or_1_out, comparator_1_gt, and_2_out);
  and and_3 (and_3_out, comparator_3_gt, comparator_4_eq);
  and and_4 (and_4_out, comparator_5_gt, comparator_6_eq);
  Hex_Digit_Display hex_digit_display_2 (.value(HH_L), .dp(1'b1));
  Hex_Digit_Display hex_digit_display_3 (.value(MM_H));  // open: dp
  and and_5 (LED_EN, comparator_8_eq, and_9_out);
  and and_6 (and_6_out, comparator_9_eq, comparator_15_eq);
  or or_2 (or_2_out, comparator_3_gt, and_3_out, comparator_4_gt);
  or or_3 (or_3_out, comparator_5_gt, and_4_out, comparator_6_gt);
  CNTR4U cntr4u_4 (
    .CLK(CLK), .LD(LED_EN), .CLR(STOP), .Q0(cntr4u_4_q0[0]), .Q1(cntr4u_4_q0[1]), .D0(1'b1), .D1(1'b0),
    .D2(1'b0), .Q2(cntr4u_4_q0[2]), .Q3(cntr4u_4_q0[3]), .D3(1'b0), .ENP(START), .ENT(START));  // open: RCO
  xor xor_1 (xor_1_out, cntr4u_4_q0[0], cntr4u_4_q0[1]);
  xor xor_2 (xor_2_out, cntr4u_4_q0[1], cntr4u_4_q0[2]);
  xor xor_3 (LED_B, cntr4u_4_q0[2], 1'b0);
  Hex_Digit_Display hex_digit_display_4 (.value(SS_H));  // open: dp
  Hex_Digit_Display hex_digit_display_5 (.value(MM_L), .dp(1'b1));
  Comparator #(.width(4)) comparator_7 (.a(HH_H), .b(4'b0010), .eq(comparator_7_eq));  // open: gt, lt
  Comparator #(.width(4)) comparator_8 (.a(MM_H), .b(4'b0101), .eq(comparator_8_eq));  // open: gt, lt
  Comparator #(.width(4)) comparator_9 (.a(SS_H), .b(4'b0101), .eq(comparator_9_eq));  // open: gt, lt
  Hex_Digit_Display hex_digit_display_6 (.value(SS_L), .dp(1'b1));
  or or_4 (or_4_out, or_1_out, or_2_out, or_3_out);
  CNTR4U cntr4u_5 (
    .CLK(CLK), .LD(and_1_out), .CLR(or_5_out), .Q0(HH_L[0]), .Q1(HH_L[1]), .D0(HH0[0]), .D1(HH0[1]),
    .D2(HH0[2]), .Q2(HH_L[2]), .Q3(HH_L[3]), .D3(HH0[3]), .ENP(LED_EN), .ENT(LED_EN));  // open: RCO
  or or_5 (or_5_out, and_8_out, and_10_out);
  CNTR4U cntr4u_6 (
    .CLK(CLK), .LD(and_1_out), .CLR(and_9_out), .Q0(MM_L[0]), .Q1(MM_L[1]), .D0(MM0[0]), .D1(MM0[1]),
    .D2(MM0[2]), .Q2(MM_L[2]), .Q3(MM_L[3]), .D3(MM0[3]), .ENP(and_6_out), .ENT(and_6_out));  // open: RCO
  CNTR4U cntr4u_7 (
    .CLK(CLK), .LD(and_1_out), .CLR(comparator_15_eq), .Q0(SS_L[0]), .Q1(SS_L[1]), .D0(SS0[0]), .D1(SS0[1]),
    .D2(SS0[2]), .Q2(SS_L[2]), .Q3(SS_L[3]), .D3(SS0[3]), .ENP(1'b1), .ENT(1'b1));  // open: RCO
  and and_7 (INErr, or_4_out, LD);
  Comparator #(.width(4)) comparator_10 (
    .a(4'b0001), .b(cntr4u_4_q0), .eq(comparator_10_eq), .lt(comparator_10_lt));  // open: gt
  or or_6 (START, comparator_10_eq, comparator_10_lt);
  Comparator #(.width(4)) comparator_11 (.a(4'b1010), .b(cntr4u_4_q0), .eq(STOP));  // open: gt, lt
  or or_7 (LED_R, and_12_out, xor_1_out, and_11_out);
  or or_8 (LED_G, and_12_out, xor_2_out);
  and and_8 (and_8_out, comparator_13_eq, LED_EN, comparator_7_eq);
  and and_9 (and_9_out, comparator_14_eq, and_6_out);
  // RGBLed RGBLED: pin names not known; wires that end beside it: LED_R, LED_G, LED_B
  Comparator #(.width(4)) comparator_12 (.a(HH_L), .b(4'b1001), .eq(comparator_12_eq));  // open: gt, lt
  Comparator #(.width(4)) comparator_13 (.a(HH_L), .b(4'b0011), .eq(comparator_13_eq));  // open: gt, lt
  and and_10 (and_10_out, comparator_12_eq, LED_EN);
  Comparator #(.width(4)) comparator_14 (.a(MM_L), .b(4'b1001), .eq(comparator_14_eq));  // open: gt, lt
  Comparator #(.width(4)) comparator_15 (.a(SS_L), .b(4'b1001), .eq(comparator_15_eq));  // open: gt, lt
  Comparator #(.width(4), .mode("unsigned")) comparator_16 (
    .a(HH_H), .b(4'b0001), .eq(comparator_16_eq));  // open: gt, lt
  Comparator #(.width(4), .mode("unsigned")) comparator_17 (
    .a(HH_L), .b(4'b0010), .eq(comparator_17_eq));  // open: gt, lt
  Comparator #(.width(4), .mode("unsigned")) comparator_18 (
    .a(MM_H), .b(4'b0011), .eq(comparator_18_eq));  // open: gt, lt
  Comparator #(.width(4), .mode("unsigned")) comparator_19 (
    .a(MM_L), .b(4'b0100), .eq(comparator_19_eq));  // open: gt, lt
  Comparator #(.width(4), .mode("unsigned")) comparator_20 (
    .a(SS_H), .b(4'b0101), .eq(comparator_20_eq));  // open: gt, lt
  Comparator #(.width(4), .mode("unsigned")) comparator_21 (
    .a(SS_L), .b(4'b0111), .eq(comparator_21_eq));  // open: gt, lt
  Comparator #(.width(4), .mode("unsigned")) comparator_22 (
    .a(SS_L), .b(4'b1000), .eq(comparator_22_eq));  // open: gt, lt
  and and_11 (and_11_out, comparator_16_eq, comparator_17_eq, comparator_18_eq, comparator_19_eq, comparator_20_eq, comparator_21_eq);
  and and_12 (and_12_out, comparator_16_eq, comparator_17_eq, comparator_18_eq, comparator_19_eq, comparator_20_eq, comparator_22_eq);

  // Other names for the same wires on the sheet: H0[3:0] = HH_L; H1[3:0] = HH_H; M0[3:0] = MM_L; M1[3:0] = MM_H;
  //   S0[3:0] = SS_L; S1[3:0] = SS_H

  // Notes on the sheet:
  //   设置初始时间BCD码
  //   输入信号
  //   请勿修改引脚名称、电路名称及电路封装外观
  //   数字时钟
  //   提示：使用4位二进制加法计数器子电路、比较器和独立逻辑门组件实现数字时钟。
  //   在载入有效时，检测设置数据错误
  //   生成三色LED显示信号，持续10个时钟周期
endmodule
