// Logisim project lab6.1.circ as structural Verilog: 1 circuit, main circuit 控制器
module \控制器  (
  input  [6:0] opcode,
  input  [2:0] funct3,
  input  [6:0] funct7,
  output [2:0] ExtOp,
  output RegWr,
  output [2:0] BandJ,
  output ALUASrc,
  output [1:0] ALUBSrc,
  output [3:0] ALUctr,
  output MemtoReg,
  output [2:0] MemOp,
  output MemWr
);

  wire and_1_out, and_2_out, and_3_out, and_4_out, and_5_out, and_6_out, and_7_out, and_8_out, and_9_out,
       and_10_out, and_11_out, and_12_out, and_13_out, and_14_out, comparator_1_eq, comparator_2_eq,
       comparator_3_eq, comparator_4_eq, comparator_5_eq, comparator_6_eq, comparator_7_eq, comparator_14_eq,
       comparator_15_eq, comparator_16_eq, comparator_17_eq, comparator_18_eq, comparator_19_eq,
       comparator_20_eq, comparator_21_eq, comparator_24_eq, comparator_25_eq, comparator_27_eq,
       comparator_28_eq, comparator_29_eq, comparator_30_eq, comparator_31_eq, comparator_32_eq,
       comparator_33_eq, comparator_34_eq, comparator_35_eq, comparator_36_eq, comparator_37_eq,
       comparator_38_eq, comparator_39_eq, comparator_40_eq, comparator_41_eq, comparator_42_eq, I, J_jalr,
       or_3_out, or_4_out, or_8_out, or_9_out, or_10_out, or_11_out, or_18_out, or_19_out, or_20_out,
       or_21_out, or_22_out, or_23_out, or_24_out, or_25_out, R, U_auipc, U_lui;

  Comparator #(.width(3), .mode("unsigned")) comparator_1 (
    .a(funct3), .b(3'b001), .eq(comparator_1_eq));  // open: gt, lt
  Comparator #(.width(3), .mode("unsigned")) comparator_2 (
    .a(funct3), .b(3'b101), .eq(comparator_2_eq));  // open: gt, lt
  Comparator #(.width(3), .mode("unsigned")) comparator_3 (
    .a(funct3), .b(3'b111), .eq(comparator_3_eq));  // open: gt, lt
  Comparator #(.width(3), .mode("unsigned")) comparator_4 (
    .a(funct3), .b(3'b100), .eq(comparator_4_eq));  // open: gt, lt
  Comparator #(.width(3), .mode("unsigned")) comparator_5 (
    .a(funct3), .b(3'b101), .eq(comparator_5_eq));  // open: gt, lt
  Comparator #(.width(3), .mode("unsigned")) comparator_6 (
    .a(funct3), .b(3'b110), .eq(comparator_6_eq));  // open: gt, lt
  Comparator #(.width(3), .mode("unsigned")) comparator_7 (
    .a(funct3), .b(3'b111), .eq(comparator_7_eq));  // open: gt, lt
  Comparator #(.width(7), .mode("unsigned")) comparator_8 (.a(opcode), .b(7'b0110111), .eq(U_lui));  // open: gt, lt
  Comparator #(.width(7), .mode("unsigned")) comparator_9 (.a(7'b1101111), .b(opcode), .eq(ExtOp[2]));  // open: gt, lt
  or or_1 (ExtOp[0], U_lui, U_auipc, BandJ[2]);
  or or_2 (ExtOp[1], BandJ[2], MemWr);
  and and_1 (and_1_out, BandJ[2], or_3_out);
  or or_3 (or_3_out, comparator_1_eq, comparator_2_eq, comparator_3_eq);
  and and_2 (and_2_out, BandJ[2], or_4_out);
  or or_4 (or_4_out, comparator_4_eq, comparator_5_eq, comparator_6_eq, comparator_7_eq);
  or or_5 (ALUASrc, U_auipc, ExtOp[2], J_jalr);
  Comparator #(.width(7), .mode("unsigned")) comparator_10 (.a(opcode), .b(7'b0010111), .eq(U_auipc));  // open: gt, lt
  Comparator #(.width(7), .mode("unsigned")) comparator_11 (.a(7'b1100111), .b(opcode), .eq(J_jalr));  // open: gt, lt
  or or_6 (BandJ[0], ExtOp[2], and_1_out);
  or or_7 (BandJ[1], J_jalr, and_2_out);
  Comparator #(.width(7), .mode("unsigned")) comparator_12 (.a(opcode), .b(7'b0010011), .eq(I));  // open: gt, lt
  Comparator #(.width(7), .mode("unsigned")) comparator_13 (.a(7'b1100011), .b(opcode), .eq(BandJ[2]));  // open: gt, lt
  Comparator #(.width(3), .mode("unsigned")) comparator_14 (
    .a(funct3), .b(3'b000), .eq(comparator_14_eq));  // open: gt, lt
  Comparator #(.width(3), .mode("unsigned")) comparator_15 (
    .a(funct3), .b(3'b100), .eq(comparator_15_eq));  // open: gt, lt
  Comparator #(.width(3), .mode("unsigned")) comparator_16 (
    .a(funct3), .b(3'b001), .eq(comparator_16_eq));  // open: gt, lt
  Comparator #(.width(3), .mode("unsigned")) comparator_17 (
    .a(funct3), .b(3'b101), .eq(comparator_17_eq));  // open: gt, lt
  Comparator #(.width(3), .mode("unsigned")) comparator_18 (
    .a(funct3), .b(3'b000), .eq(comparator_18_eq));  // open: gt, lt
  Comparator #(.width(3), .mode("unsigned")) comparator_19 (
    .a(funct3), .b(3'b001), .eq(comparator_19_eq));  // open: gt, lt
  Comparator #(.width(3), .mode("unsigned")) comparator_20 (
    .a(funct3), .b(3'b000), .eq(comparator_20_eq));  // open: gt, lt
  Comparator #(.width(3), .mode("unsigned")) comparator_21 (
    .a(funct3), .b(3'b001), .eq(comparator_21_eq));  // open: gt, lt
  Comparator #(.width(7), .mode("unsigned")) comparator_22 (.a(opcode), .b(7'b0110011), .eq(R));  // open: gt, lt
  Comparator #(.width(7), .mode("unsigned")) comparator_23 (.a(7'b0000011), .b(opcode), .eq(MemtoReg));  // open: gt, lt
  and and_3 (and_3_out, MemWr, comparator_24_eq);
  Comparator #(.width(3), .mode("unsigned")) comparator_24 (
    .a(funct3), .b(3'b000), .eq(comparator_24_eq));  // open: gt, lt
  and and_4 (and_4_out, MemtoReg, or_8_out);
  or or_8 (or_8_out, comparator_14_eq, comparator_15_eq);
  and and_5 (and_5_out, MemWr, comparator_25_eq);
  Comparator #(.width(3), .mode("unsigned")) comparator_25 (
    .a(funct3), .b(3'b001), .eq(comparator_25_eq));  // open: gt, lt
  and and_6 (and_6_out, MemtoReg, or_9_out);
  or or_9 (or_9_out, comparator_16_eq, comparator_17_eq);
  and and_7 (and_7_out, MemWr, or_10_out);
  or or_10 (or_10_out, comparator_18_eq, comparator_19_eq);
  and and_8 (and_8_out, MemtoReg, or_11_out);
  or or_11 (or_11_out, comparator_20_eq, comparator_21_eq);
  Comparator #(.width(7), .mode("unsigned")) comparator_26 (.a(opcode), .b(7'b0100011), .eq(MemWr));  // open: gt, lt
  or or_12 (RegWr, U_lui, U_auipc, I, R, ExtOp[2], J_jalr, MemtoReg);
  or or_13 (MemOp[0], and_3_out, and_4_out);
  or or_14 (MemOp[1], and_5_out, and_6_out);
  or or_15 (MemOp[2], and_7_out, and_8_out);
  or or_16 (ALUBSrc[0], ExtOp[2], J_jalr);
  or or_17 (ALUBSrc[1], U_lui, U_auipc, I, MemtoReg, MemWr);
  Comparator #(.width(3), .mode("unsigned")) comparator_27 (
    .a(funct3), .b(3'b011), .eq(comparator_27_eq));  // open: gt, lt
  Comparator #(.width(3), .mode("unsigned")) comparator_28 (
    .a(funct3), .b(3'b111), .eq(comparator_28_eq));  // open: gt, lt
  Comparator #(.width(3), .mode("unsigned")) comparator_29 (
    .a(funct3), .b(3'b001), .eq(comparator_29_eq));  // open: gt, lt
  Comparator #(.width(3), .mode("unsigned")) comparator_30 (
    .a(funct3), .b(3'b101), .eq(comparator_30_eq));  // open: gt, lt
  Comparator #(.width(3), .mode("unsigned")) comparator_31 (
    .a(funct3), .b(3'b111), .eq(comparator_31_eq));  // open: gt, lt
  Comparator #(.width(3), .mode("unsigned")) comparator_32 (
    .a(funct3), .b(3'b110), .eq(comparator_32_eq));  // open: gt, lt
  Comparator #(.width(3), .mode("unsigned")) comparator_33 (
    .a(funct3), .b(3'b010), .eq(comparator_33_eq));  // open: gt, lt
  Comparator #(.width(3), .mode("unsigned")) comparator_34 (
    .a(funct3), .b(3'b011), .eq(comparator_34_eq));  // open: gt, lt
  Comparator #(.width(3), .mode("unsigned")) comparator_35 (
    .a(funct3), .b(3'b110), .eq(comparator_35_eq));  // open: gt, lt
  Comparator #(.width(3), .mode("unsigned")) comparator_36 (
    .a(funct3), .b(3'b111), .eq(comparator_36_eq));  // open: gt, lt
  Comparator #(.width(3), .mode("unsigned")) comparator_37 (
    .a(funct3), .b(3'b100), .eq(comparator_37_eq));  // open: gt, lt
  Comparator #(.width(3), .mode("unsigned")) comparator_38 (
    .a(funct3), .b(3'b101), .eq(comparator_38_eq));  // open: gt, lt
  Comparator #(.width(3), .mode("unsigned")) comparator_39 (
    .a(funct3), .b(3'b110), .eq(comparator_39_eq));  // open: gt, lt
  Comparator #(.width(3), .mode("unsigned")) comparator_40 (
    .a(funct3), .b(3'b111), .eq(comparator_40_eq));  // open: gt, lt
  Comparator #(.width(3), .mode("unsigned")) comparator_41 (
    .a(funct3), .b(3'b101), .eq(comparator_41_eq));  // open: gt, lt
  Comparator #(.width(3), .mode("unsigned")) comparator_42 (
    .a(funct3), .b(3'b000), .eq(comparator_42_eq));  // open: gt, lt
  or or_18 (or_18_out, R, I);
  and and_9 (and_9_out, or_18_out, or_19_out);
  or or_19 (or_19_out, comparator_27_eq, comparator_28_eq, comparator_29_eq, comparator_30_eq);
  and and_10 (and_10_out, BandJ[2], or_20_out);
  or or_20 (or_20_out, comparator_31_eq, comparator_32_eq);
  or or_21 (or_21_out, R, I);
  and and_11 (and_11_out, or_21_out, or_22_out);
  or or_22 (or_22_out, comparator_33_eq, comparator_34_eq, comparator_35_eq, comparator_36_eq);
  or or_23 (or_23_out, R, I);
  and and_12 (and_12_out, or_23_out, or_24_out);
  or or_24 (or_24_out, comparator_37_eq, comparator_38_eq, comparator_39_eq, comparator_40_eq);
  or or_25 (or_25_out, I, R);
  and and_13 (and_13_out, or_25_out, comparator_41_eq, funct7[5]);
  and and_14 (and_14_out, R, comparator_42_eq, funct7[5]);
  or or_26 (ALUctr[0], and_9_out, U_lui, and_10_out);
  or or_27 (ALUctr[1], and_11_out, U_lui, BandJ[2]);
  or or_28 (ALUctr[2], and_12_out, U_lui);
  or or_29 (ALUctr[3], and_13_out, U_lui, and_14_out);

  // Other names for the same wires on the sheet: B = BandJ[2]; J_jal = ExtOp[2]; L = MemtoReg; S = MemWr

  // Notes on the sheet:
  //   输入引脚
  //   请勿修改引脚名称、电路名称及电路封装外观
  //   提示：根据指令种类，把7位指令code用一位指令类型标志位来表示，再通过功能码来区分具体指令，生成控制信号。
  //   输出引脚
endmodule
