// Logisim project lab6.2.circ as structural Verilog: 17 circuits, main circuit main
module main (
  input  ReSet,
  input  [31:0] Init_Addr,
  input  clk,
  output [31:0] PC,
  output [31:0] IR,
  output [31:0] BusW,
  output [31:0] Din,
  output [15:0] Cycles,
  output Halt
);

  wire ALUASrc, clk_out, clk_t, MemtoReg, MemWr, not_2_out, NPCASrc, NPCBSrc, RegWr, Zero;
  wire [1:0] ALUBSrc;
  wire [2:0] BandJ, ExtOp, Funt3, MemOp;
  wire [3:0] ALUctr;
  wire [6:0] Funt7, OpCode;
  wire [31:0] alu_1_s, BusA, DataA, DataB, dataram_1_dataout, idu_1_busb, Imm;

  Clock u_clk (.out(clk_out));
  not not_1 (clk_t, clk_out);
  IFU ifu_1 (
    .Initial_Address(Init_Addr), .Imm(Imm), .BusA(BusA), .PC(PC), .CLK(clk_t), .Reset(ReSet),
    .NxtASrc(NPCASrc), .NxtBSrc(NPCBSrc), .halt(Halt));
  ROM #(.addrWidth(16), .dataWidth(32), .Select("high")) rom_1 (.addr(PC[17:2]), .data(IR));
  \控制器  \u_控制器_1  (
    .opcode(OpCode), .ExtOp(ExtOp), .RegWr(RegWr), .BandJ(BandJ), .funct3(Funt3), .ALUASrc(ALUASrc),
    .ALUBSrc(ALUBSrc), .ALUctr(ALUctr), .funct7(Funt7), .MemtoReg(MemtoReg), .MemOp(MemOp), .MemWr(MemWr),
    .Halt(Halt));
  IDU idu_1 (
    .IR(IR), .BusW(BusW), .PC(PC), .DataA(DataA), .DataB(DataB), .BusA(BusA), .BusB(idu_1_busb),
    .OpCode(OpCode), .ExtOp(ExtOp), .RegWr(RegWr), .Imm(Imm), .Funct3(Funt3), .ALUASrc(ALUASrc),
    .ALUBSrc(ALUBSrc), .Funct7(Funt7), .CLK(clk_t));
  Multiplexer #(.width(32), .enable("false")) multiplexer_1 (.in0(idu_1_busb), .out(Din), .sel(ReSet));  // open: in1
  ALU alu_1 (.ALUctr(ALUctr), .Zero(Zero), .A(DataA), .B(DataB), .S(alu_1_s));
  BandJ bandj_1 (.Branch(BandJ), .NxtASrc(NPCASrc), .Zero(Zero), .NxtBSrc(NPCBSrc), .Result0(alu_1_s[0]));
  DataRAM dataram_1 (
    .CLK(clk_t), .CLR(1'b0), .WE(MemWr), .MemOp(MemOp), .Addr(alu_1_s[17:0]), .Din(Din),
    .DataOut(dataram_1_dataout));  // open: AlignErr
  // Probe on Cycles
  Counter #(.width(16), .max('hffff), .behavior("old")) \u_计数器  (
    .count(not_2_out), .Q(Cycles), .clk(clk_t), .clr(ReSet));  // open: load, D, carry, preset
  not not_2 (not_2_out, Halt);
  Multiplexer #(.width(32), .enable("false")) multiplexer_2 (
    .in0(alu_1_s), .in1(dataram_1_dataout), .out(BusW), .sel(MemtoReg));

  // Notes on the sheet:
  //   输入引脚
  //   contents of rom_1 (hex, n*v repeats v):
  //   413 9117 ffc10113 2ec000ef 259693 d50833 50313 82883 60513 8c5d863 261793 f307b3 7a783 fff50713
  //   271713 e30733 70613 ffc70713 2f8d463 fff50513 472783 fea5c6e3 d30833 f82023 58513 f62023 1182023
  //   8067 d30833 251613 f82023 c30633 4a5d063 468713 e30733 70813 158593 470713 ffc72783 fca584e3
  //   fef8d6e3 f62023 2a5d063 259693 f85ff06f 58513 1182023 8067 58513 fa1ff06f 259813 1030833 58513
  //   f95ff06f 1ec5da63 fa010113 4812c23 5512223 3712e23 4112e23 4912a23 5212823 5312623 5412423 5612023
  //   3812c23 3912a23 3a12823 3b12623 58b93 60a93 50413 a8613 b8593 40513 ee5ff0ef a12223 fff50c93
  //   159bd663 c8613 b8593 40513 ec9ff0ef a12423 fff50d13 13abd263 d0613 b8593 40513 eadff0ef a12623
  //   fff50d93 fbbde63 d8613 b8593 40513 e91ff0ef a12823 fff50993 d3bda63 98613 b8593 40513 e75ff0ef
  //   fff50913 50493 b2bd863 90613 b8593 40513 e59ff0ef fff50b13 50a13 96bd663 b0613 b8593 40513 e3dff0ef
  //   a12a23 fff50c13 78bd263 c0613 b8593 40513 e21ff0ef fff50813 50713 50bd063 80613 b8593 40513 e12e23
  //   1012c23 dfdff0ef 50893 b8593 fff50613 40513 188b93 eadff0ef 1812803 1c12703 fd0bc4e3 170b93 fb8bc2e3
  //   1412783 178b93 f76bcee3 1a0b93 f52bcce3 148b93 f33bcae3 1012783 178b93 f1bbc6e3 c12783 178b93
  //   efabc2e3 812783 178b93 eb9bcee3 412783 178b93 e95bcae3 5c12083 5812403 5412483 5012903 4c12983
  //   4812a03 4412a83 4012b03 3c12b83 3812c03 3412c83 3012d03 2c12d83 6010113 8067 8067 ff010113 31400513
  //   1300613 593 112623 df5ff0ef c12083 513 1010113 8067 ff010113 31000513 112623 fcdff0ef 36a02223 73 0
  //   4e20 1d4c0 53724e00 5b8d80 13d620 5dc 9896800 186a0 0 2bf20 2af8 b532b80 15f90 3e8 46 32 61a80
  //   2dc6c0 1f40 aa deadbeef
  //   请勿修改引脚名称、电路名称及电路封装外观
  //   指令存储器和数据存储器数据位都是32位，指令存储器编址以字为单位，数据存储器编址以字节为单位。
  //   引用取指令部件、取操作数部件、ALU部件、数据存储器、分支控制器、指令存储器等部件，完成单周期CPU设计。
  //   输出引脚
  //   状态元件的触发条件都设置成上升沿触发，时钟输入信号通过反相器输入。
  //   程序执行周期数
endmodule

module BandJ (
  input  [2:0] Branch,
  input  Zero,
  input  Result0,
  output NxtASrc,
  output NxtBSrc
);

  wire not_1_out, not_2_out, or_1_out;

  not not_1 (not_1_out, Result0);
  or or_1 (or_1_out, not_1_out, Zero);
  Multiplexer #(.select(3), .enable("false")) multiplexer_1 (
    .in0(1'b0), .in1(1'b1), .in2(1'b1), .in4(Zero), .in5(not_2_out), .in6(Result0), .in7(or_1_out),
    .out(NxtBSrc), .sel(Branch));  // open: in3
  not not_2 (not_2_out, Zero);
  Multiplexer #(.select(3), .enable("false")) multiplexer_2 (
    .in0(1'b0), .in1(1'b0), .in2(1'b1), .in4(1'b0), .in5(1'b0), .in6(1'b0), .in7(1'b0), .out(NxtASrc),
    .sel(Branch));  // open: in3

  // Notes on the sheet:
  //   Branch: pull=down
  //   Zero: pull=down
  //   输入信号
  //   请勿修改引脚名称、电路名称及电路封装外观
  //   不要修改控制信号的编码定义、引脚名称和在布局中的位置。
  //   输出信号
endmodule

module IFU (
  input  [31:0] Initial_Address,
  input  [31:0] Imm,
  input  [31:0] BusA,
  input  CLK,
  input  Reset,
  input  halt,
  input  NxtASrc,
  input  NxtBSrc,
  output [31:0] PC
);

  wire [31:0] adder_1_out, multiplexer_1_out, multiplexer_2_out, multiplexer_3_out;

  Multiplexer #(.width(32), .enable("false")) multiplexer_1 (
    .in0(PC), .in1(BusA), .out(multiplexer_1_out), .sel(NxtASrc));
  Multiplexer #(.width(32), .enable("false")) multiplexer_2 (
    .in0(32'h4), .in1(Imm), .out(multiplexer_2_out), .sel(NxtBSrc));
  Adder #(.width(32)) adder_1 (.a(multiplexer_1_out), .b(multiplexer_2_out), .out(adder_1_out));  // open: cin, cout
  Multiplexer #(.width(32), .enable("false")) multiplexer_3 (
    .in0(adder_1_out), .in1(Initial_Address), .out(multiplexer_3_out), .sel(Reset));
  Register #(.width(32), .Select("low")) u_PC (
    .D(multiplexer_3_out), .Q(PC), .clk(CLK), .cs(halt));  // open: en, clr, preset
  ROM #(.addrWidth(16), .dataWidth(32), .Select("low")) rom_1 (.addr(PC[17:2]));  // open: data

  // Other names for the same wires on the sheet: Init_Addr[31:0] = Initial_Address

  // Notes on the sheet:
  //   NxtBSrc: pull=down
  //   Imm: pull=down
  //   BusA: pull=down
  //   NxtASrc: pull=down
  //   输入信号
  //   请勿修改引脚名称、电路名称及电路封装外观
  //   指令存储器256KB，数据位为32位，地址位为16位。PC寄存器数据宽度32位，片选信号高电平有效
  //   输出信号
endmodule

module \控制器  (
  input  [6:0] opcode,
  input  [2:0] funct3,
  input  [6:0] funct7,
  output [2:0] ExtOp,
  output RegWr,
  output [2:0] BandJ,
  output ALUASrc,
  output [1:0] ALUBSrc,
  output [3:0] ALUctr,
  output MemtoReg,
  output [2:0] MemOp,
  output MemWr,
  output Halt
);

  wire and_1_out, and_2_out, and_3_out, and_4_out, and_5_out, and_6_out, and_7_out, and_8_out, and_9_out,
       and_10_out, and_11_out, and_12_out, and_13_out, and_14_out, comparator_1_eq, comparator_2_eq,
       comparator_3_eq, comparator_4_eq, comparator_5_eq, comparator_6_eq, comparator_7_eq, comparator_14_eq,
       comparator_15_eq, comparator_16_eq, comparator_17_eq, comparator_18_eq, comparator_19_eq,
       comparator_20_eq, comparator_21_eq, comparator_24_eq, comparator_25_eq, comparator_28_eq,
       comparator_29_eq, comparator_30_eq, comparator_31_eq, comparator_32_eq, comparator_33_eq,
       comparator_34_eq, comparator_35_eq, comparator_36_eq, comparator_37_eq, comparator_38_eq,
       comparator_39_eq, comparator_40_eq, comparator_41_eq, comparator_42_eq, comparator_43_eq, I, J_jalr,
       or_3_out, or_4_out, or_8_out, or_9_out, or_10_out, or_11_out, or_18_out, or_19_out, or_20_out,
       or_21_out, or_22_out, or_23_out, or_24_out, or_25_out, R, U_auipc, U_lui;

  Comparator #(.width(3), .mode("unsigned")) comparator_1 (
    .a(funct3), .b(3'b001), .eq(comparator_1_eq));  // open: gt, lt
  Comparator #(.width(3), .mode("unsigned")) comparator_2 (
    .a(funct3), .b(3'b101), .eq(comparator_2_eq));  // open: gt, lt
  Comparator #(.width(3), .mode("unsigned")) comparator_3 (
    .a(funct3), .b(3'b111), .eq(comparator_3_eq));  // open: gt, lt
  Comparator #(.width(3), .mode("unsigned")) comparator_4 (
    .a(funct3), .b(3'b100), .eq(comparator_4_eq));  // open: gt, lt
  Comparator #(.width(3), .mode("unsigned")) comparator_5 (
    .a(funct3), .b(3'b101), .eq(comparator_5_eq));  // open: gt, lt
  Comparator #(.width(3), .mode("unsigned")) comparator_6 (
    .a(funct3), .b(3'b110), .eq(comparator_6_eq));  // open: gt, lt
  Comparator #(.width(3), .mode("unsigned")) comparator_7 (
    .a(funct3), .b(3'b111), .eq(comparator_7_eq));  // open: gt, lt
  Comparator #(.width(7), .mode("unsigned")) comparator_8 (.a(opcode), .b(7'b0110111), .eq(U_lui));  // open: gt, lt
  Comparator #(.width(7), .mode("unsigned")) comparator_9 (.a(7'b1101111), .b(opcode), .eq(ExtOp[2]));  // open: gt, lt
  or or_1 (ExtOp[0], U_lui, U_auipc, BandJ[2]);
  or or_2 (ExtOp[1], BandJ[2], MemWr);
  and and_1 (and_1_out, BandJ[2], or_3_out);
  or or_3 (or_3_out, comparator_1_eq, comparator_2_eq, comparator_3_eq);
  and and_2 (and_2_out, BandJ[2], or_4_out);
  or or_4 (or_4_out, comparator_4_eq, comparator_5_eq, comparator_6_eq, comparator_7_eq);
  or or_5 (ALUASrc, U_auipc, ExtOp[2], J_jalr);
  Comparator #(.width(7), .mode("unsigned")) comparator_10 (.a(opcode), .b(7'b0010111), .eq(U_auipc));  // open: gt, lt
  Comparator #(.width(7), .mode("unsigned")) comparator_11 (.a(7'b1100111), .b(opcode), .eq(J_jalr));  // open: gt, lt
  or or_6 (BandJ[0], ExtOp[2], and_1_out);
  or or_7 (BandJ[1], J_jalr, and_2_out);
  Comparator #(.width(7), .mode("unsigned")) comparator_12 (.a(opcode), .b(7'b0010011), .eq(I));  // open: gt, lt
  Comparator #(.width(7), .mode("unsigned")) comparator_13 (.a(7'b1100011), .b(opcode), .eq(BandJ[2]));  // open: gt, lt
  Comparator #(.width(3), .mode("unsigned")) comparator_14 (
    .a(funct3), .b(3'b000), .eq(comparator_14_eq));  // open: gt, lt
  Comparator #(.width(3), .mode("unsigned")) comparator_15 (
    .a(funct3), .b(3'b100), .eq(comparator_15_eq));  // open: gt, lt
  Comparator #(.width(3), .mode("unsigned")) comparator_16 (
    .a(funct3), .b(3'b001), .eq(comparator_16_eq));  // open: gt, lt
  Comparator #(.width(3), .mode("unsigned")) comparator_17 (
    .a(funct3), .b(3'b101), .eq(comparator_17_eq));  // open: gt, lt
  Comparator #(.width(3), .mode("unsigned")) comparator_18 (
    .a(funct3), .b(3'b000), .eq(comparator_18_eq));  // open: gt, lt
  Comparator #(.width(3), .mode("unsigned")) comparator_19 (
    .a(funct3), .b(3'b001), .eq(comparator_19_eq));  // open: gt, lt
  Comparator #(.width(3), .mode("unsigned")) comparator_20 (
    .a(funct3), .b(3'b000), .eq(comparator_20_eq));  // open: gt, lt
  Comparator #(.width(3), .mode("unsigned")) comparator_21 (
    .a(funct3), .b(3'b001), .eq(comparator_21_eq));  // open: gt, lt
  Comparator #(.width(7), .mode("unsigned")) comparator_22 (.a(opcode), .b(7'b0110011), .eq(R));  // open: gt, lt
  Comparator #(.width(7), .mode("unsigned")) comparator_23 (.a(7'b0000011), .b(opcode), .eq(MemtoReg));  // open: gt, lt
  and and_3 (and_3_out, MemWr, comparator_24_eq);
  Comparator #(.width(3), .mode("unsigned")) comparator_24 (
    .a(funct3), .b(3'b000), .eq(comparator_24_eq));  // open: gt, lt
  and and_4 (and_4_out, MemtoReg, or_8_out);
  or or_8 (or_8_out, comparator_14_eq, comparator_15_eq);
  and and_5 (and_5_out, MemWr, comparator_25_eq);
  Comparator #(.width(3), .mode("unsigned")) comparator_25 (
    .a(funct3), .b(3'b001), .eq(comparator_25_eq));  // open: gt, lt
  and and_6 (and_6_out, MemtoReg, or_9_out);
  or or_9 (or_9_out, comparator_16_eq, comparator_17_eq);
  and and_7 (and_7_out, MemWr, or_10_out);
  or or_10 (or_10_out, comparator_18_eq, comparator_19_eq);
  and and_8 (and_8_out, MemtoReg, or_11_out);
  or or_11 (or_11_out, comparator_20_eq, comparator_21_eq);
  Comparator #(.width(7), .mode("unsigned")) comparator_26 (.a(opcode), .b(7'b0100011), .eq(MemWr));  // open: gt, lt
  Comparator #(.width(7), .mode("unsigned")) comparator_27 (.a(opcode), .b(7'b1110011), .eq(Halt));  // open: gt, lt
  or or_12 (RegWr, U_lui, U_auipc, I, R, ExtOp[2], J_jalr, MemtoReg);
  or or_13 (MemOp[0], and_3_out, and_4_out);
  or or_14 (MemOp[1], and_5_out, and_6_out);
  or or_15 (MemOp[2], and_7_out, and_8_out);
  or or_16 (ALUBSrc[0], ExtOp[2], J_jalr);
  or or_17 (ALUBSrc[1], U_lui, U_auipc, I, MemtoReg, MemWr);
  Comparator #(.width(3), .mode("unsigned")) comparator_28 (
    .a(funct3), .b(3'b011), .eq(comparator_28_eq));  // open: gt, lt
  Comparator #(.width(3), .mode("unsigned")) comparator_29 (
    .a(funct3), .b(3'b111), .eq(comparator_29_eq));  // open: gt, lt
  Comparator #(.width(3), .mode("unsigned")) comparator_30 (
    .a(funct3), .b(3'b001), .eq(comparator_30_eq));  // open: gt, lt
  Comparator #(.width(3), .mode("unsigned")) comparator_31 (
    .a(funct3), .b(3'b101), .eq(comparator_31_eq));  // open: gt, lt
  Comparator #(.width(3), .mode("unsigned")) comparator_32 (
    .a(funct3), .b(3'b111), .eq(comparator_32_eq));  // open: gt, lt
  Comparator #(.width(3), .mode("unsigned")) comparator_33 (
    .a(funct3), .b(3'b110), .eq(comparator_33_eq));  // open: gt, lt
  Comparator #(.width(3), .mode("unsigned")) comparator_34 (
    .a(funct3), .b(3'b010), .eq(comparator_34_eq));  // open: gt, lt
  Comparator #(.width(3), .mode("unsigned")) comparator_35 (
    .a(funct3), .b(3'b011), .eq(comparator_35_eq));  // open: gt, lt
  Comparator #(.width(3), .mode("unsigned")) comparator_36 (
    .a(funct3), .b(3'b110), .eq(comparator_36_eq));  // open: gt, lt
  Comparator #(.width(3), .mode("unsigned")) comparator_37 (
    .a(funct3), .b(3'b111), .eq(comparator_37_eq));  // open: gt, lt
  Comparator #(.width(3), .mode("unsigned")) comparator_38 (
    .a(funct3), .b(3'b100), .eq(comparator_38_eq));  // open: gt, lt
  Comparator #(.width(3), .mode("unsigned")) comparator_39 (
    .a(funct3), .b(3'b101), .eq(comparator_39_eq));  // open: gt, lt
  Comparator #(.width(3), .mode("unsigned")) comparator_40 (
    .a(funct3), .b(3'b110), .eq(comparator_40_eq));  // open: gt, lt
  Comparator #(.width(3), .mode("unsigned")) comparator_41 (
    .a(funct3), .b(3'b111), .eq(comparator_41_eq));  // open: gt, lt
  Comparator #(.width(3), .mode("unsigned")) comparator_42 (
    .a(funct3), .b(3'b101), .eq(comparator_42_eq));  // open: gt, lt
  Comparator #(.width(3), .mode("unsigned")) comparator_43 (
    .a(funct3), .b(3'b000), .eq(comparator_43_eq));  // open: gt, lt
  or or_18 (or_18_out, R, I);
  and and_9 (and_9_out, or_18_out, or_19_out);
  or or_19 (or_19_out, comparator_28_eq, comparator_29_eq, comparator_30_eq, comparator_31_eq);
  and and_10 (and_10_out, BandJ[2], or_20_out);
  or or_20 (or_20_out, comparator_32_eq, comparator_33_eq);
  or or_21 (or_21_out, R, I);
  and and_11 (and_11_out, or_21_out, or_22_out);
  or or_22 (or_22_out, comparator_34_eq, comparator_35_eq, comparator_36_eq, comparator_37_eq);
  or or_23 (or_23_out, R, I);
  and and_12 (and_12_out, or_23_out, or_24_out);
  or or_24 (or_24_out, comparator_38_eq, comparator_39_eq, comparator_40_eq, comparator_41_eq);
  or or_25 (or_25_out, I, R);
  and and_13 (and_13_out, or_25_out, comparator_42_eq, funct7[5]);
  and and_14 (and_14_out, R, comparator_43_eq, funct7[5]);
  or or_26 (ALUctr[0], and_9_out, U_lui, and_10_out);
  or or_27 (ALUctr[1], and_11_out, U_lui, BandJ[2]);
  or or_28 (ALUctr[2], and_12_out, U_lui);
  or or_29 (ALUctr[3], and_13_out, U_lui, and_14_out);

  // Other names for the same wires on the sheet: B = BandJ[2]; J_jal = ExtOp[2]; L = MemtoReg; S = MemWr

  // Notes on the sheet:
  //   输入引脚
  //   请勿修改引脚名称、电路名称及电路封装外观
  //   提示：根据指令种类，把7位指令code用一位指令类型标志位来表示，再通过功能码来区分具体指令，生成控制信号。
  //   输出引脚
endmodule

module IDU (
  input  [31:0] IR,
  input  [31:0] BusW,
  input  [31:0] PC,
  input  [2:0] ExtOp,
  input  RegWr,
  input  ALUASrc,
  input  [1:0] ALUBSrc,
  input  CLK,
  output [31:0] DataA,
  output [31:0] DataB,
  output [31:0] BusA,
  output [31:0] BusB,
  output [6:0] OpCode,
  output [31:0] Imm,
  output [2:0] Funct3,
  output [6:0] Funct7
);

  \立即数扩展器  \u_立即数扩展器_1  (.Instr(IR), .Extop(ExtOp), .imm(Imm));
  RegFile regfile_1 (
    .R1_num(IR[19:15]), .R2_num(IR[24:20]), .Write_Reg_num(IR[11:7]), .Din(BusW), .Reg1Out(BusA),
    .Reg2Out(BusB), .Write_Enable(RegWr), .Clock(CLK));
  Multiplexer #(.width(32), .enable("false")) multiplexer_1 (.in0(BusA), .in1(PC), .out(DataA), .sel(ALUASrc));
  Multiplexer #(.select(2), .width(32), .enable("false")) multiplexer_2 (
    .in0(BusB), .in1(32'h4), .in2(Imm), .out(DataB), .sel(ALUBSrc));  // open: in3

  assign Funct3 = IR[14:12];
  assign Funct7 = IR[31:25];
  assign OpCode = IR[6:0];

  // Other names for the same wires on the sheet: op[6:0] = IR[6:0]

  // Notes on the sheet:
  //   ExtOp: pull=down
  //   ALUASrc: pull=down
  //   RegWr: pull=down
  //   ALUBSrc: pull=down
  //   BusW: pull=down
  //   PC: pull=down
  //   输入信号
  //   为了后续实验中的引用，不要修改ALUASrc、ALUBSrc和EXtOP编码定义。
  //   请勿修改引脚名称、电路名称及电路封装外观
  //   输出信号
  //   修改寄存器堆电路设计，0号寄存器始终为0。
endmodule

module RegFile (
  input  [4:0] R1_num,
  input  [4:0] R2_num,
  input  [4:0] Write_Reg_num,
  input  [31:0] Din,
  input  Write_Enable,
  input  Clock,
  output [31:0] Reg1Out,
  output [31:0] Reg2Out
);

  wire and_1_out, and_2_out, and_3_out, and_4_out, and_5_out, and_6_out, and_7_out, and_8_out, and_9_out,
       and_10_out, and_11_out, and_12_out, and_13_out, and_14_out, and_15_out, and_16_out, and_17_out,
       and_18_out, and_19_out, and_20_out, and_21_out, and_22_out, and_23_out, and_24_out, and_25_out,
       and_26_out, and_27_out, and_28_out, and_29_out, and_30_out, and_31_out, and_32_out, decoder_1_out0,
       decoder_1_out1, decoder_1_out2, decoder_1_out3, decoder_1_out4, decoder_1_out5, decoder_1_out6,
       decoder_1_out7, decoder_1_out8, decoder_1_out9, decoder_1_out10, decoder_1_out11, decoder_1_out12,
       decoder_1_out13, decoder_1_out14, decoder_1_out15, decoder_1_out16, decoder_1_out17, decoder_1_out18,
       decoder_1_out19, decoder_1_out20, decoder_1_out21, decoder_1_out22, decoder_1_out23, decoder_1_out24,
       decoder_1_out25, decoder_1_out26, decoder_1_out27, decoder_1_out28, decoder_1_out29, decoder_1_out30,
       decoder_1_out31;
  wire [31:0] _0_q, _1_q, _2_q, _3_q, _4_q, _5_q, _6_q, _7_q, _8_q, _9_q, _10_q, _11_q, _12_q, _13_q, _14_q,
       _15_q, _16_q, _17_q, _18_q, _19_q, _20_q, _21_q, _22_q, _23_q, _24_q, _25_q, _26_q, _27_q, _28_q,
       _29_q, _30_q, _31_q;

  Decoder #(.select(5), .enable("false")) decoder_1 (
    .out0(decoder_1_out0), .out1(decoder_1_out1), .out2(decoder_1_out2), .out3(decoder_1_out3),
    .out4(decoder_1_out4), .out5(decoder_1_out5), .out6(decoder_1_out6), .out7(decoder_1_out7),
    .out8(decoder_1_out8), .out9(decoder_1_out9), .out10(decoder_1_out10), .out11(decoder_1_out11),
    .out12(decoder_1_out12), .out13(decoder_1_out13), .out14(decoder_1_out14), .out15(decoder_1_out15),
    .out16(decoder_1_out16), .out17(decoder_1_out17), .out18(decoder_1_out18), .out19(decoder_1_out19),
    .out20(decoder_1_out20), .out21(decoder_1_out21), .out22(decoder_1_out22), .out23(decoder_1_out23),
    .out24(decoder_1_out24), .out25(decoder_1_out25), .out26(decoder_1_out26), .out27(decoder_1_out27),
    .out28(decoder_1_out28), .out29(decoder_1_out29), .out30(decoder_1_out30), .out31(decoder_1_out31),
    .sel(Write_Reg_num));
  and and_1 (and_1_out, decoder_1_out0, Write_Enable);
  and and_2 (and_2_out, decoder_1_out1, Write_Enable);
  and and_3 (and_3_out, decoder_1_out2, Write_Enable);
  and and_4 (and_4_out, decoder_1_out3, Write_Enable);
  and and_5 (and_5_out, decoder_1_out4, Write_Enable);
  and and_6 (and_6_out, decoder_1_out5, Write_Enable);
  and and_7 (and_7_out, decoder_1_out6, Write_Enable);
  and and_8 (and_8_out, decoder_1_out7, Write_Enable);
  and and_9 (and_9_out, decoder_1_out8, Write_Enable);
  and and_10 (and_10_out, decoder_1_out9, Write_Enable);
  and and_11 (and_11_out, decoder_1_out10, Write_Enable);
  and and_12 (and_12_out, decoder_1_out11, Write_Enable);
  and and_13 (and_13_out, decoder_1_out12, Write_Enable);
  and and_14 (and_14_out, decoder_1_out13, Write_Enable);
  and and_15 (and_15_out, decoder_1_out14, Write_Enable);
  and and_16 (and_16_out, decoder_1_out15, Write_Enable);
  and and_17 (and_17_out, decoder_1_out16, Write_Enable);
  and and_18 (and_18_out, decoder_1_out17, Write_Enable);
  and and_19 (and_19_out, decoder_1_out18, Write_Enable);
  and and_20 (and_20_out, decoder_1_out19, Write_Enable);
  and and_21 (and_21_out, decoder_1_out20, Write_Enable);
  and and_22 (and_22_out, decoder_1_out21, Write_Enable);
  and and_23 (and_23_out, decoder_1_out22, Write_Enable);
  and and_24 (and_24_out, decoder_1_out23, Write_Enable);
  and and_25 (and_25_out, decoder_1_out24, Write_Enable);
  and and_26 (and_26_out, decoder_1_out25, Write_Enable);
  and and_27 (and_27_out, decoder_1_out26, Write_Enable);
  and and_28 (and_28_out, decoder_1_out27, Write_Enable);
  and and_29 (and_29_out, decoder_1_out28, Write_Enable);
  and and_30 (and_30_out, decoder_1_out29, Write_Enable);
  and and_31 (and_31_out, decoder_1_out30, Write_Enable);
  and and_32 (and_32_out, decoder_1_out31, Write_Enable);
  Register #(.width(32), .Select("high")) _0 (.D({32{1'b0}}), .en(and_1_out), .Q(_0_q), .clk(Clock));  // open: clr
  Register #(.width(32), .Select("high")) _1 (.D(Din), .en(and_2_out), .Q(_1_q), .clk(Clock));  // open: clr
  Register #(.width(32), .Select("high")) _2 (.D(Din), .en(and_3_out), .Q(_2_q), .clk(Clock));  // open: clr
  Register #(.width(32), .Select("high")) _3 (.D(Din), .en(and_4_out), .Q(_3_q), .clk(Clock));  // open: clr
  Register #(.width(32), .Select("high")) _4 (.D(Din), .en(and_5_out), .Q(_4_q), .clk(Clock));  // open: clr
  Register #(.width(32), .Select("high")) _5 (.D(Din), .en(and_6_out), .Q(_5_q), .clk(Clock));  // open: clr
  Register #(.width(32), .Select("high")) _6 (.D(Din), .en(and_7_out), .Q(_6_q), .clk(Clock));  // open: clr
  Register #(.width(32), .Select("high")) _7 (.D(Din), .en(and_8_out), .Q(_7_q), .clk(Clock));  // open: clr
  Register #(.width(32), .Select("high")) _8 (.D(Din), .en(and_9_out), .Q(_8_q), .clk(Clock));  // open: clr
  Register #(.width(32), .Select("high")) _9 (.D(Din), .en(and_10_out), .Q(_9_q), .clk(Clock));  // open: clr
  Register #(.width(32), .Select("high")) _10 (.D(Din), .en(and_11_out), .Q(_10_q), .clk(Clock));  // open: clr
  Register #(.width(32), .Select("high")) _11 (.D(Din), .en(and_12_out), .Q(_11_q), .clk(Clock));  // open: clr
  Register #(.width(32), .Select("high")) _12 (.D(Din), .en(and_13_out), .Q(_12_q), .clk(Clock));  // open: clr
  Register #(.width(32), .Select("high")) _13 (.D(Din), .en(and_14_out), .Q(_13_q), .clk(Clock));  // open: clr
  Register #(.width(32), .Select("high")) _14 (.D(Din), .en(and_15_out), .Q(_14_q), .clk(Clock));  // open: clr
  Register #(.width(32), .Select("high")) _15 (.D(Din), .en(and_16_out), .Q(_15_q), .clk(Clock));  // open: clr
  Register #(.width(32), .Select("high")) _16 (.D(Din), .en(and_17_out), .Q(_16_q), .clk(Clock));  // open: clr
  Register #(.width(32), .Select("high")) _17 (.D(Din), .en(and_18_out), .Q(_17_q), .clk(Clock));  // open: clr
  Register #(.width(32), .Select("high")) _18 (.D(Din), .en(and_19_out), .Q(_18_q), .clk(Clock));  // open: clr
  Register #(.width(32), .Select("high")) _19 (.D(Din), .en(and_20_out), .Q(_19_q), .clk(Clock));  // open: clr
  Register #(.width(32), .Select("high")) _20 (.D(Din), .en(and_21_out), .Q(_20_q), .clk(Clock));  // open: clr
  Register #(.width(32), .Select("high")) _21 (.D(Din), .en(and_22_out), .Q(_21_q), .clk(Clock));  // open: clr
  Register #(.width(32), .Select("high")) _22 (.D(Din), .en(and_23_out), .Q(_22_q), .clk(Clock));  // open: clr
  Register #(.width(32), .Select("high")) _23 (.D(Din), .en(and_24_out), .Q(_23_q), .clk(Clock));  // open: clr
  Register #(.width(32), .Select("high")) _24 (.D(Din), .en(and_25_out), .Q(_24_q), .clk(Clock));  // open: clr
  Register #(.width(32), .Select("high")) _25 (.D(Din), .en(and_26_out), .Q(_25_q), .clk(Clock));  // open: clr
  Register #(.width(32), .Select("high")) _26 (.D(Din), .en(and_27_out), .Q(_26_q), .clk(Clock));  // open: clr
  Register #(.width(32), .Select("high")) _27 (.D(Din), .en(and_28_out), .Q(_27_q), .clk(Clock));  // open: clr
  Register #(.width(32), .Select("high")) _28 (.D(Din), .en(and_29_out), .Q(_28_q), .clk(Clock));  // open: clr
  Register #(.width(32), .Select("high")) _29 (.D(Din), .en(and_30_out), .Q(_29_q), .clk(Clock));  // open: clr
  Register #(.width(32), .Select("high")) _30 (.D(Din), .en(and_31_out), .Q(_30_q), .clk(Clock));  // open: clr
  Register #(.width(32), .Select("high")) _31 (.D(Din), .en(and_32_out), .Q(_31_q), .clk(Clock));  // open: clr
  Multiplexer #(.select(5), .width(32), .enable("false")) multiplexer_1 (
    .in0(_0_q), .in1(_1_q), .in2(_2_q), .in3(_3_q), .in4(_4_q), .in5(_5_q), .in6(_6_q), .in7(_7_q),
    .in8(_8_q), .in9(_9_q), .in10(_10_q), .in11(_11_q), .in12(_12_q), .in13(_13_q), .in14(_14_q),
    .in15(_15_q), .in16(_16_q), .in17(_17_q), .in18(_18_q), .in19(_19_q), .in20(_20_q), .in21(_21_q),
    .in22(_22_q), .in23(_23_q), .in24(_24_q), .in25(_25_q), .in26(_26_q), .in27(_27_q), .in28(_28_q),
    .in29(_29_q), .in30(_30_q), .in31(_31_q), .out(Reg1Out), .sel(R1_num));
  Multiplexer #(.select(5), .width(32), .enable("false")) multiplexer_2 (
    .in0(_0_q), .in1(_1_q), .in2(_2_q), .in3(_3_q), .in4(_4_q), .in5(_5_q), .in6(_6_q), .in7(_7_q),
    .in8(_8_q), .in9(_9_q), .in10(_10_q), .in11(_11_q), .in12(_12_q), .in13(_13_q), .in14(_14_q),
    .in15(_15_q), .in16(_16_q), .in17(_17_q), .in18(_18_q), .in19(_19_q), .in20(_20_q), .in21(_21_q),
    .in22(_22_q), .in23(_23_q), .in24(_24_q), .in25(_25_q), .in26(_26_q), .in27(_27_q), .in28(_28_q),
    .in29(_29_q), .in30(_30_q), .in31(_31_q), .out(Reg2Out), .sel(R2_num));

  // Other names for the same wires on the sheet: CLK = Clock; RA[4:0] = R1_num; RB[4:0] = R2_num; RDA[31:0] = Reg1Out;
  //   RDB[31:0] = Reg2Out; RW[4:0] = Write_Reg_num; WE = Write_Enable

  // Notes on the sheet:
  //   输入引脚
  //   请勿修改引脚名称、电路名称及电路封装外观
  //   提示：使用译码器、多路选择器和32位寄存器及逻辑门实现寄存器堆，禁止直接使用存储器组件。
  //   输出引脚
endmodule

module \立即数扩展器  (
  input  [31:0] Instr,
  input  [2:0] Extop,
  output [31:0] imm
);

  wire [11:0] bit_extender_4_out;
  wire [19:0] bit_extender_3_out;
  wire [31:0] bit_extender_1_out, bit_extender_2_out;

  assign bit_extender_1_out = {{20{Instr[31]}}, Instr[31:20]};  // Bit_Extender bit_extender_1
  assign bit_extender_2_out = {{20{Instr[31]}}, {Instr[31:25], Instr[11:7]}};  // Bit_Extender bit_extender_2
  assign bit_extender_3_out = {{19{Instr[31]}}, Instr[31]};  // Bit_Extender bit_extender_3
  assign bit_extender_4_out = {{11{Instr[31]}}, Instr[31]};  // Bit_Extender bit_extender_4
  Multiplexer #(.select(3), .width(32), .enable("false")) multiplexer_1 (
    .in0(bit_extender_1_out), .in1({Instr[31:12], {12{1'b0}}}), .in2(bit_extender_2_out),
    .in3({bit_extender_3_out, Instr[7], Instr[30:25], Instr[11:8], 1'b0}),
    .in4({bit_extender_4_out, Instr[19:12], Instr[20], Instr[30:21], 1'b0}), .out(imm), .sel(Extop));  // open: in5, in6, in7

  // Notes on the sheet:
  //   Instr: pull=down
  //   Extop: pull=down
  //   输入引脚
  //   请勿修改引脚名称、电路名称及电路封装外观
  //   提示：使用分线器和多路选择器实现立即数扩展器
  //   输出引脚
endmodule

module DataRAM (
  input  CLK,
  input  CLR,
  input  WE,
  input  [2:0] MemOp,
  input  [17:0] Addr,
  input  [31:0] Din,
  output AlignErr,
  output [31:0] DataOut
);

  wire [3:0] SEL;
  wire [7:0] D0, D1, D2, D3, multiplexer_4_out;
  wire [15:0] multiplexer_5_out;
  wire [31:0] bit_extender_1_out, bit_extender_2_out, bit_extender_3_out, bit_extender_4_out, RESULT;

  Multiplexer #(.select(3), .width(8), .enable("false")) multiplexer_1 (
    .in0(Din[7:0]), .in4(Din[15:8]), .in7(Din[31:24]), .out(D3), .sel(SEL[2:0]));  // open: in1, in2, in3, in5, in6
  RAM #(.addrWidth(16), .bus("separate"), .Select("high"), .simpleMode("false")) ram_1 (
    .addr(Addr[17:2]), .din(D3), .data(RESULT[31:24]), .str(WE), .sel(SEL[3]), .clk(CLK), .clr(CLR));  // open: ld
  SEL sel_1 (
    .Mem2(MemOp[2]), .Mem1(MemOp[1]), .Mem0(MemOp[0]), .Addr1(Addr[1]), .Addr0(Addr[0]), .Sel3(SEL[3]),
    .Sel2(SEL[2]), .Sel1(SEL[1]), .Sel0(SEL[0]));
  and and_1 (AlignErr, ~SEL[3], ~SEL[2], ~SEL[1], ~SEL[0]);  // AND_Gate
  Multiplexer #(.select(3), .width(8), .enable("false")) multiplexer_2 (
    .in0(Din[7:0]), .in4(Din[7:0]), .in7(Din[23:16]), .out(D2), .sel({SEL[3], SEL[1:0]}));  // open: in1, in2, in3, in5, in6
  RAM #(.addrWidth(16), .bus("separate"), .Select("high"), .simpleMode("false")) ram_2 (
    .addr(Addr[17:2]), .din(D2), .data(RESULT[23:16]), .str(WE), .sel(SEL[2]), .clk(CLK), .clr(CLR));  // open: ld
  Multiplexer #(.select(3), .width(8), .enable("false")) multiplexer_3 (
    .in0(Din[7:0]), .in1(Din[15:8]), .in7(Din[15:8]), .out(D1), .sel({SEL[3:2], SEL[0]}));  // open: in2, in3, in4, in5, in6
  RAM #(.addrWidth(16), .bus("separate"), .Select("high"), .simpleMode("false")) ram_3 (
    .addr(Addr[17:2]), .din(D1), .data(RESULT[15:8]), .str(WE), .sel(SEL[1]), .clk(CLK), .clr(CLR));  // open: ld
  Multiplexer #(.select(2), .width(8), .enable("false")) multiplexer_4 (
    .in0(RESULT[7:0]), .in1(RESULT[15:8]), .in2(RESULT[23:16]), .in3(RESULT[31:24]), .out(multiplexer_4_out),
    .sel(Addr[1:0]));
  Multiplexer #(.width(16), .enable("false")) multiplexer_5 (
    .in0(RESULT[15:0]), .in1(RESULT[31:16]), .out(multiplexer_5_out), .sel(Addr[1]));
  Multiplexer #(.select(3), .width(8), .enable("false")) multiplexer_6 (
    .in0(Din[7:0]), .in1(Din[7:0]), .in7(Din[7:0]), .out(D0), .sel(SEL[3:1]));  // open: in2, in3, in4, in5, in6
  assign bit_extender_1_out = {{24{1'b0}}, multiplexer_4_out};  // Bit_Extender bit_extender_1
  assign bit_extender_2_out = {{24{multiplexer_4_out[7]}}, multiplexer_4_out};  // Bit_Extender bit_extender_2
  assign bit_extender_3_out = {{16{1'b0}}, multiplexer_5_out};  // Bit_Extender bit_extender_3
  assign bit_extender_4_out = {{16{multiplexer_5_out[15]}}, multiplexer_5_out};  // Bit_Extender bit_extender_4
  RAM #(.addrWidth(16), .bus("separate"), .Select("high"), .simpleMode("false")) ram_4 (
    .addr(Addr[17:2]), .din(D0), .data(RESULT[7:0]), .str(WE), .sel(SEL[0]), .clk(CLK), .clr(CLR));  // open: ld
  Multiplexer #(.select(3), .width(32), .enable("false")) multiplexer_7 (
    .in0(RESULT), .in1(bit_extender_1_out), .in2(bit_extender_3_out), .in5(bit_extender_2_out),
    .in6(bit_extender_4_out), .out(DataOut), .sel(MemOp));  // open: in3, in4, in7

  // Other names for the same wires on the sheet: Dout[31:0] = DataOut

  // Notes on the sheet:
  //   输入引脚
  //   请勿修改引脚名称、电路名称及电路封装外观
  //   为了后续实验中的引用，不要修改MemOp的编码定义、引脚名称和在布局中的位置。
  //   32位数据存储器，按字节分4片存储，可按照字节、半字和字进行存储；读取字节或半字时，支持0扩展和符号位扩展。
  //   输出引脚
endmodule

module ALU (
  input  [3:0] ALUctr,
  input  [31:0] A,
  input  [31:0] B,
  output Zero,
  output [31:0] S
);

  wire adder32_1_cf, adder32_1_of, adder32_1_sf, aluctrl_1_alctr, aluctrl_1_lrctr, aluctrl_1_sigctr,
       aluctrl_1_subctr, multiplexer_1_out, xor_3_out;
  wire [2:0] aluctrl_1_opctr;
  wire [31:0] adder32_1_s, and_1_out, bit_extender_1_out, bit_extender_2_out, or_1_out, shifter32_1_dataout,
       xor_1_out, xor_2_out;

  assign bit_extender_1_out = {{31{aluctrl_1_subctr}}, aluctrl_1_subctr};  // Bit_Extender bit_extender_1
  Adder32 adder32_1 (
    .CF(adder32_1_cf), .Cin(aluctrl_1_subctr), .OF(adder32_1_of), .SF(adder32_1_sf), .S(adder32_1_s), .X(A),
    .Y(xor_1_out), .ZF(Zero));  // open: Cout
  assign xor_1_out = B ^ bit_extender_1_out;  // XOR_Gate xor_1, 32 bits wide
  assign and_1_out = A & B;  // AND_Gate and_1, 32 bits wide
  assign or_1_out = A | B;  // OR_Gate or_1, 32 bits wide
  assign xor_2_out = A ^ B;  // XOR_Gate xor_2, 32 bits wide
  Shifter32 shifter32_1 (
    .shamt(B[4:0]), .L_R(aluctrl_1_lrctr), .A_L(aluctrl_1_alctr), .DataIn(A), .DataOut(shifter32_1_dataout));
  Multiplexer #(.enable("false")) multiplexer_1 (
    .in0(adder32_1_cf), .in1(xor_3_out), .out(multiplexer_1_out), .sel(aluctrl_1_sigctr));
  xor xor_3 (xor_3_out, adder32_1_of, adder32_1_sf);
  // Probe on A
  // Probe on B
  // Probe on S
  Multiplexer #(.select(3), .width(32), .enable("false")) multiplexer_2 (
    .in0(adder32_1_s), .in1(and_1_out), .in2(or_1_out), .in3(xor_2_out), .in4(shifter32_1_dataout), .in5(B),
    .in6(bit_extender_2_out), .out(S), .sel(aluctrl_1_opctr));  // open: in7
  ALUctrl aluctrl_1 (
    .SUBctr(aluctrl_1_subctr), .LRctr(aluctrl_1_lrctr), .ALUctr(ALUctr), .SIGctr(aluctrl_1_sigctr),
    .ALctr(aluctrl_1_alctr), .OPctr(aluctrl_1_opctr));
  assign bit_extender_2_out = {{31{1'b0}}, multiplexer_1_out};  // Bit_Extender bit_extender_2

  // Other names for the same wires on the sheet: Result[31:0] = S

  // Notes on the sheet:
  //   ALUctr: pull=down
  //   B: pull=down
  //   A: pull=down
  //   输入引脚
  //   请勿修改引脚名称、电路名称及电路封装外观
  //   提示：使用32位并行加法器子电路、桶形移位器、ALU控制子电路实现32位ALU
  //   功能说明:32位ALU，输入32位操作数A、B，4位控制信号ALUctr，输出32位结果Reseult和1位Zero标志位
  //   输出引脚
  //   操作数和结果
endmodule

module ALUctrl (
  input  [3:0] ALUctr,
  output SUBctr,
  output LRctr,
  output SIGctr,
  output ALctr,
  output [2:0] OPctr
);

  wire and_1_out, and_2_out, and_6_out, and_7_out, and_8_out, and_9_out, and_10_out, and_11_out, and_12_out,
       not_1_out, not_2_out, not_3_out, not_4_out;

  not not_1 (not_1_out, ALUctr[0]);
  not not_2 (not_2_out, ALUctr[1]);
  not not_3 (not_3_out, ALUctr[2]);
  not not_4 (not_4_out, ALUctr[3]);
  and and_1 (and_1_out, not_4_out, not_3_out, ALUctr[1]);
  and and_2 (and_2_out, ALUctr[3], not_3_out, not_2_out, not_1_out);
  and and_3 (SIGctr, not_4_out, not_3_out, ALUctr[1], not_1_out);
  and and_4 (ALctr, ALUctr[3], ALUctr[2], not_2_out, ALUctr[0]);
  and and_5 (LRctr, not_4_out, not_3_out, not_2_out, ALUctr[0]);
  and and_6 (and_6_out, not_4_out, ALUctr[2], not_2_out, not_1_out);
  and and_7 (and_7_out, ALUctr[2], ALUctr[1], ALUctr[0]);
  and and_8 (and_8_out, not_4_out, not_3_out, ALUctr[1]);
  and and_9 (and_9_out, not_4_out, ALUctr[2], not_1_out);
  and and_10 (and_10_out, not_4_out, not_3_out, ALUctr[1]);
  and and_11 (and_11_out, not_4_out, not_2_out, ALUctr[0]);
  and and_12 (and_12_out, ALUctr[3], ALUctr[2], ALUctr[0]);
  or or_1 (SUBctr, and_1_out, and_2_out);
  or or_2 (OPctr[0], and_6_out, and_7_out);
  or or_3 (OPctr[1], and_8_out, and_9_out);
  or or_4 (OPctr[2], and_10_out, and_11_out, and_12_out);

  // Notes on the sheet:
  //   输入引脚
  //   ALU操作控制信号生成部件
  //   A3\
  //   A3
  //   A0\
  //   A1\
  //   A2\
  //   输出引脚
  //   A0
  //   A1
  //   A2
endmodule

module Adder32 (
  input  Cin,
  input  [31:0] X,
  input  [31:0] Y,
  output CF,
  output Cout,
  output OF,
  output SF,
  output [31:0] S,
  output ZF
);

  wire adder16_2_c16, and_1_out, and_2_out, not_1_out, not_2_out, not_3_out, or_2_out;

  xor xor_1 (CF, Cin, Cout);
  Adder16 adder16_1 (.C0(adder16_2_c16), .C16(Cout), .X(X[31:16]), .Y(Y[31:16]), .S(S[31:16]));  // open: Pg, Gg
  Adder16 adder16_2 (.C0(Cin), .C16(adder16_2_c16), .X(X[15:0]), .Y(Y[15:0]), .S(S[15:0]));  // open: Pg, Gg
  not not_1 (not_1_out, X[31]);
  not not_2 (not_2_out, Y[31]);
  not not_3 (not_3_out, S[31]);
  and and_1 (and_1_out, S[31], not_1_out, not_2_out);
  and and_2 (and_2_out, X[31], Y[31], not_3_out);
  or or_1 (OF, and_1_out, and_2_out);
  // Probe on X
  // Probe on Y
  // Probe on S
  or or_2 (or_2_out, S[0], S[1], S[2], S[3], S[4], S[5], S[6], S[7], S[8], S[9], S[10], S[11], S[12], S[13], S[14], S[15], S[16], S[17], S[18], S[19], S[20], S[21], S[22], S[23], S[24], S[25], S[26], S[27], S[28], S[29], S[30], S[31]);
  not not_4 (ZF, or_2_out);

  assign SF = S[31];

  // Notes on the sheet:
  //   Cin: pull=down
  //   Y: pull=down
  //   X: pull=down
  //   输入引脚区
  //   输出引脚区
  //   请勿修改引脚名称、电路名称及电路封装外观
  //   提示：使用16位并行加法器子电路实现32位快速加法器
  //   功能说明:32位Adder  S=X+Y，Cout为最高位进位位，Cin为进位输入， S为和，溢出OF、进位CF、零ZF、符号SF。
  //   +
  //   =
  //   无符号加法
endmodule

// 移位器
module Shifter32 (
  input  [4:0] shamt,
  input  L_R,
  input  A_L,
  input  [31:0] DataIn,
  output [31:0] DataOut
);

  wire [0:0] multiplexer_2_out;
  wire [1:0] multiplexer_3_out_2, multiplexer_4_out;
  wire [3:0] multiplexer_6_out;
  wire [7:0] multiplexer_7_out_2, multiplexer_8_out;
  wire [15:0] multiplexer_10_out;
  wire [23:0] multiplexer_7_out;
  wire [29:0] multiplexer_3_out;
  wire [31:0] multiplexer_5_out, multiplexer_9_out;
  wire [31:16] multiplexer_9_out_2;

  Multiplexer #(.enable("false")) multiplexer_1 (.in0(1'b0), .in1(DataIn[31]), .out(multiplexer_9_out[31]), .sel(A_L));
  Multiplexer #(.enable("false")) multiplexer_2 (.in0(1'b0), .in1(DataIn[31]), .out(multiplexer_2_out[0]), .sel(A_L));
  Multiplexer #(.select(2), .width(32), .enable("false")) multiplexer_3 (
    .in0(DataIn), .in1({multiplexer_9_out[31], DataIn[31:1]}), .in2(DataIn),
    .in3({DataIn[30:0], multiplexer_2_out[0]}), .out({multiplexer_3_out, multiplexer_3_out_2}),
    .sel({L_R, shamt[0]}));
  Multiplexer #(.width(2), .enable("false")) multiplexer_4 (
    .in0(2'b00), .in1(multiplexer_3_out[29:28]), .out(multiplexer_4_out), .sel(A_L));
  Multiplexer #(.select(2), .width(32), .enable("false")) multiplexer_5 (
    .in0({multiplexer_3_out, multiplexer_3_out_2}), .in1({{2{multiplexer_9_out[31]}}, multiplexer_3_out}),
    .in2({multiplexer_3_out, multiplexer_3_out_2}),
    .in3({multiplexer_3_out[27:0], multiplexer_3_out_2, multiplexer_4_out}), .out(multiplexer_5_out),
    .sel({L_R, shamt[1]}));
  Multiplexer #(.width(4), .enable("false")) multiplexer_6 (
    .in0(4'b0000), .in1(multiplexer_5_out[31:28]), .out(multiplexer_6_out), .sel(A_L));
  Multiplexer #(.select(2), .width(32), .enable("false")) multiplexer_7 (
    .in0(multiplexer_5_out), .in1({{4{multiplexer_9_out[31]}}, multiplexer_5_out[31:4]}),
    .in2(multiplexer_5_out), .in3({multiplexer_5_out[27:0], multiplexer_6_out}),
    .out({multiplexer_7_out, multiplexer_7_out_2}), .sel({L_R, shamt[2]}));
  Multiplexer #(.width(8), .enable("false")) multiplexer_8 (
    .in0({8{1'b0}}), .in1(multiplexer_7_out[23:16]), .out(multiplexer_8_out), .sel(A_L));
  Multiplexer #(.select(2), .width(32), .enable("false")) multiplexer_9 (
    .in0({multiplexer_7_out, multiplexer_7_out_2}), .in1({{8{multiplexer_9_out[31]}}, multiplexer_7_out}),
    .in2({multiplexer_7_out, multiplexer_7_out_2}),
    .in3({multiplexer_7_out[15:0], multiplexer_7_out_2, multiplexer_8_out}),
    .out({multiplexer_9_out[15:0], multiplexer_9_out_2}), .sel({L_R, shamt[3]}));
  Multiplexer #(.width(16), .enable("false")) multiplexer_10 (
    .in0({16{1'b0}}), .in1(multiplexer_9_out[15:0]), .out(multiplexer_10_out), .sel(A_L));
  Multiplexer #(.select(2), .width(32), .enable("false")) multiplexer_11 (
    .in0({multiplexer_9_out[15:0], multiplexer_9_out_2}),
    .in1({{16{multiplexer_9_out[31]}}, multiplexer_9_out[15:0]}),
    .in2({multiplexer_9_out[15:0], multiplexer_9_out_2}), .in3({multiplexer_9_out_2, multiplexer_10_out}),
    .out(DataOut), .sel({L_R, shamt[4]}));

  // Other names for the same wires on the sheet: Din[31:0] = DataIn; Left_Right = L_R; Arth_Logic = A_L;
  //   Dout[31:0] = DataOut

  // Notes on the sheet:
  //   L/R,A/L: 00逻辑右移，01算术右移，10逻辑左移，11：循环左移
  //   输入引脚
  //   请勿修改引脚名称、电路名称及电路封装外观
  //   提示：使用多路选择器、逻辑门实现32位桶形移位器，禁止直接使用移位器组件。
  //   输出引脚
endmodule

module Adder16 (
  input  C0,
  input  [15:0] X,
  input  [15:0] Y,
  output C16,
  output Pg,
  output Gg,
  output [15:0] S
);

  wire cla4_1_gg, cla4_1_pg, cla4_2_gg, cla4_2_pg, cla4_3_gg, cla4_3_pg, cla4_4_gg, cla4_4_pg, clu4_1_c1,
       clu4_1_c2, clu4_1_c3;

  CLA4 cla4_1 (
    .X(X[15:12]), .F(S[15:12]), .Y(Y[15:12]), .Pg(cla4_1_pg), .Cin(clu4_1_c3), .Gg(cla4_1_gg));  // open: Cout
  CLA4 cla4_2 (.X(X[11:8]), .F(S[11:8]), .Y(Y[11:8]), .Pg(cla4_2_pg), .Cin(clu4_1_c2), .Gg(cla4_2_gg));  // open: Cout
  CLU4 clu4_1 (
    .P0(cla4_4_pg), .P1(cla4_3_pg), .P2(cla4_2_pg), .P3(cla4_1_pg), .C1(clu4_1_c1), .C3(clu4_1_c3),
    .G0(cla4_4_gg), .G1(cla4_3_gg), .G2(cla4_2_gg), .G3(cla4_1_gg), .C2(clu4_1_c2), .C4(C16), .C0(C0),
    .Pg(Pg), .Gg(Gg));
  CLA4 cla4_3 (.X(X[7:4]), .F(S[7:4]), .Y(Y[7:4]), .Pg(cla4_3_pg), .Cin(clu4_1_c1), .Gg(cla4_3_gg));  // open: Cout
  CLA4 cla4_4 (.X(X[3:0]), .F(S[3:0]), .Y(Y[3:0]), .Pg(cla4_4_pg), .Cin(C0), .Gg(cla4_4_gg));  // open: Cout
  // Probe on X
  // Probe on Y
  // Probe on S

  // Notes on the sheet:
  //   C0: pull=down
  //   X: pull=down
  //   Y: pull=down
  //   输入引脚区
  //   请勿修改引脚名称、电路名称及电路封装外观
  //   提示：使用4位先行进位加法器和CLU子电路实现16位并行加法器
  //   功能说明:16位Adder  S=X+Y，C16为最高位进位位，C0为进位输入， Pg、Gg为成组进位生成传递函数
  //   输出引脚区
  //   +
  //   =
  //   无符号加法
endmodule

module CLA4 (
  input  [3:0] X,
  input  [3:0] Y,
  input  Cin,
  output [3:0] F,
  output Cout,
  output Pg,
  output Gg
);

  wire clu4_1_c1, clu4_1_c2, clu4_1_c3, fa_1_g, fa_1_p, fa_2_g, fa_2_p, fa_3_g, fa_3_p, fa_4_g, fa_4_p;

  FA fa_1 (.A(X[3]), .F(F[3]), .B(Y[3]), .P(fa_1_p), .Cin(clu4_1_c3), .G(fa_1_g));
  Hex_Digit_Display hex_digit_display_1 (.value(X));  // open: dp
  Hex_Digit_Display hex_digit_display_2 (.value(Y));  // open: dp
  FA fa_2 (.A(X[2]), .F(F[2]), .B(Y[2]), .P(fa_2_p), .Cin(clu4_1_c2), .G(fa_2_g));
  Hex_Digit_Display hex_digit_display_3 (.value(F));  // open: dp
  CLU4 clu4_1 (
    .P0(fa_4_p), .P1(fa_3_p), .P2(fa_2_p), .P3(fa_1_p), .C1(clu4_1_c1), .C3(clu4_1_c3), .G0(fa_4_g),
    .G1(fa_3_g), .G2(fa_2_g), .G3(fa_1_g), .C2(clu4_1_c2), .C4(Cout), .C0(Cin), .Pg(Pg), .Gg(Gg));
  FA fa_3 (.A(X[1]), .F(F[1]), .B(Y[1]), .P(fa_3_p), .Cin(clu4_1_c1), .G(fa_3_g));
  FA fa_4 (.A(X[0]), .F(F[0]), .B(Y[0]), .P(fa_4_p), .Cin(Cin), .G(fa_4_g));

  // Other names for the same wires on the sheet: Z[3:0] = F

  // Notes on the sheet:
  //   +
  //   =
  //   输出
  //   输入
  //   请勿修改引脚名称、电路名称及电路封装外观
  //   提示：使用全加器和CLU子电路实现四位先行进位加法器CLA4
endmodule

module CLU4 (
  input  P0,
  input  P1,
  input  P2,
  input  P3,
  input  G0,
  input  G1,
  input  G2,
  input  G3,
  input  C0,
  output C1,
  output C3,
  output C2,
  output C4,
  output Pg,
  output Gg
);

  wire and_1_out, and_3_out, and_4_out, and_5_out, and_6_out, and_7_out, and_8_out, and_9_out, and_10_out,
       and_11_out;

  or or_1 (C4, Gg, and_1_out);
  and and_1 (and_1_out, Pg, C0);
  and and_2 (Pg, P0, P1, P2, P3);
  and and_3 (and_3_out, P2, G1);
  or or_2 (C3, G2, and_3_out, and_4_out, and_5_out);
  and and_4 (and_4_out, P2, P1, G0);
  and and_5 (and_5_out, P2, P1, P0, C0);
  and and_6 (and_6_out, P1, G0);
  or or_3 (C2, G1, and_6_out, and_7_out);
  and and_7 (and_7_out, P1, P0, C0);
  or or_4 (Gg, G3, and_8_out, and_10_out, and_11_out);
  and and_8 (and_8_out, P3, G2);
  or or_5 (C1, G0, and_9_out);
  and and_9 (and_9_out, P0, C0);
  and and_10 (and_10_out, P3, P2, G1);
  and and_11 (and_11_out, P3, P2, P1, G0);

  // Notes on the sheet:
  //   输入引脚
  //   请勿修改引脚名称、电路名称及电路封装外观
  //   提示：使用逻辑门电路实现4位四位先行进位部件CLU，Pg、Gg为成组进位生成传递函数
  //   输出引脚
endmodule

module FA (
  input  A,
  input  B,
  input  Cin,
  output F,
  output P,
  output G
);

  wire xor_2_out;

  xor xor_1 (F, A, xor_2_out);
  xor xor_2 (xor_2_out, B, Cin);
  or or_1 (P, A, B);
  and and_1 (G, A, B);

  // Notes on the sheet:
  //   输入引脚
  //   请勿修改引脚名称、电路名称及电路封装外观
  //   全加器
  //   输出引脚
endmodule

module SEL (
  input  Mem2,
  input  Mem1,
  input  Mem0,
  input  Addr1,
  input  Addr0,
  output Sel3,
  output Sel2,
  output Sel1,
  output Sel0
);

  wire and_1_out, and_2_out, and_3_out, and_4_out, and_5_out, and_6_out, and_7_out, and_8_out, and_9_out,
       and_10_out, and_11_out, and_12_out, not_1_out, not_2_out, not_3_out, not_4_out, not_5_out, not_6_out,
       not_7_out, not_8_out, not_9_out, not_10_out, not_11_out, not_12_out, not_13_out, not_14_out,
       not_15_out, not_16_out, not_17_out, not_18_out, not_19_out, not_20_out, not_21_out, not_22_out,
       not_23_out, not_24_out, not_25_out, not_26_out, not_27_out, not_28_out, not_29_out, not_30_out,
       not_31_out, not_32_out, not_33_out, not_34_out, not_35_out, not_36_out;

  not not_1 (not_1_out, Mem2);
  not not_2 (not_2_out, Mem1);
  not not_3 (not_3_out, Mem0);
  not not_4 (not_4_out, Addr1);
  not not_5 (not_5_out, Addr0);
  not not_6 (not_6_out, Mem1);
  not not_7 (not_7_out, Mem0);
  not not_8 (not_8_out, Addr0);
  not not_9 (not_9_out, Mem2);
  not not_10 (not_10_out, Mem1);
  not not_11 (not_11_out, Mem0);
  not not_12 (not_12_out, Addr1);
  not not_13 (not_13_out, Addr0);
  not not_14 (not_14_out, Mem1);
  not not_15 (not_15_out, Addr0);
  not not_16 (not_16_out, Mem0);
  not not_17 (not_17_out, Addr0);
  not not_18 (not_18_out, Mem2);
  not not_19 (not_19_out, Mem0);
  not not_20 (not_20_out, Addr1);
  not not_21 (not_21_out, Addr0);
  not not_22 (not_22_out, Mem1);
  not not_23 (not_23_out, Addr1);
  not not_24 (not_24_out, Mem0);
  not not_25 (not_25_out, Addr1);
  not not_26 (not_26_out, Addr0);
  not not_27 (not_27_out, Mem2);
  not not_28 (not_28_out, Mem1);
  not not_29 (not_29_out, Addr1);
  not not_30 (not_30_out, Addr0);
  not not_31 (not_31_out, Mem1);
  not not_32 (not_32_out, Addr1);
  not not_33 (not_33_out, Addr0);
  not not_34 (not_34_out, Mem0);
  not not_35 (not_35_out, Addr1);
  not not_36 (not_36_out, Addr0);
  and and_1 (and_1_out, not_1_out, not_2_out, not_3_out, not_4_out, not_5_out);
  and and_2 (and_2_out, not_6_out, Mem0, Addr1, Addr0);
  and and_3 (and_3_out, Mem1, not_7_out, Addr1, not_8_out);
  and and_4 (and_4_out, not_9_out, not_10_out, not_11_out, not_12_out, not_13_out);
  and and_5 (and_5_out, not_14_out, Mem0, Addr1, not_15_out);
  and and_6 (and_6_out, Mem1, not_16_out, Addr1, not_17_out);
  and and_7 (and_7_out, not_18_out, not_19_out, not_20_out, not_21_out);
  and and_8 (and_8_out, not_22_out, Mem0, not_23_out, Addr0);
  and and_9 (and_9_out, Mem1, not_24_out, not_25_out, not_26_out);
  and and_10 (and_10_out, not_27_out, not_28_out, not_29_out, not_30_out);
  and and_11 (and_11_out, not_31_out, Mem0, not_32_out, not_33_out);
  and and_12 (and_12_out, Mem1, not_34_out, not_35_out, not_36_out);
  or or_1 (Sel3, and_1_out, and_2_out, and_3_out);
  or or_2 (Sel2, and_4_out, and_5_out, and_6_out);
  or or_3 (Sel1, and_7_out, and_8_out, and_9_out);
  or or_4 (Sel0, and_10_out, and_11_out, and_12_out);
endmodule
